// Logisim project LABORATORNAY2.circ as structural Verilog: 5 circuits, main circuit Структурная схема кодека
module \Структурная_схема_кодека  (
  input  e1,
  input  e2,
  input  i1,
  input  e3,
  input  e4,
  input  i2,
  input  e5,
  input  i3,
  input  e6,
  input  e7,
  input  i4,
  input  e8,
  input  i5,
  input  e9,
  input  e10,
  input  e11,
  input  e12,
  input  e13,
  input  e14,
  input  e15,
  input  e16,
  output \с1 ,
  output \с1_star ,
  output i1_star,
  output \с2 ,
  output \с2_star ,
  output i2_star,
  output \с3 ,
  output \с3_star ,
  output \с4 ,
  output \с4_star ,
  output i3_star,
  output \с5 ,
  output \с5_star ,
  output i4_star,
  output \с6 ,
  output \с6_star ,
  output \с7 ,
  output \с7_star ,
  output i5_star,
  output \с8 ,
  output \с8_star ,
  output \с9 ,
  output \с9_star ,
  output \с10 ,
  output \с10_star ,
  output \с11 ,
  output \с11_star ,
  output \с12 ,
  output \с12_star ,
  output \с13 ,
  output \с13_star ,
  output \с14 ,
  output \с14_star ,
  output \с15 ,
  output \с15_star ,
  output \с16 ,
  output \с16_star 
);

  wire \функциональная_схема_мажоритарного_декодера_1_out_5 ;
  wire [15:0] \функциональная_схема_канала_1_out_34 , \функциональная_схема_кодера_1_out_22 ;

  \Функциональная_схема_кодера  \u_функциональная_схема_кодера_1  (
    .i1(i1), .i2(i2), .i3(i3), .i4(i4), .i5(i5), .c1(\с1 ), .c2(\с2 ), .c3(\с3 ), .c4(\с4 ), .c5(\с5 ),
    .c6(\с6 ), .c7(\с7 ), .c8(\с8 ), .c9(\с9 ), .c10(\с10 ), .c11(\с11 ), .c12(\с12 ), .c13(\с13 ),
    .c14(\с14 ), .c15(\с15 ), .c16(\с16 ), .out_22(\функциональная_схема_кодера_1_out_22 ));
  \Функциональная_схема_канала  \u_функциональная_схема_канала_1  (
    .e1(e1), .e2(e2), .e3(e3), .e4(e4), .e5(e5), .e6(e6), .e7(e7), .e8(e8), .e9(e9), .e10(e10), .e11(e11),
    .e12(e12), .e13(e13), .e14(e14), .e15(e15), .e16(e16), .in_17(\функциональная_схема_кодера_1_out_22 ),
    .c1_star(\с1_star ), .c2_star(\с2_star ), .c3_star(\с3_star ), .c4_star(\с4_star ), .c5_star(\с5_star ),
    .c6_star(\с6_star ), .c7_star(\с7_star ), .c8_star(\с8_star ), .c9_star(\с9_star ),
    .c10_star(\с10_star ), .c11_star(\с11_star ), .c12_star(\с12_star ), .c13_star(\с13_star ),
    .c14_star(\с14_star ), .c15_star(\с15_star ), .c16_star(\с16_star ),
    .out_34(\функциональная_схема_канала_1_out_34 ));
  \Функциональная_схема_мажоритарного_декодера  \u_функциональная_схема_мажоритарного_декодера_1  (
    .in_1(\функциональная_схема_канала_1_out_34 ), .i1_star(i1_star),
    .out_5(\функциональная_схема_мажоритарного_декодера_1_out_5 ), .out_2(i2_star), .out_4(i3_star),
    .out_6(i4_star), .out_7(i5_star));
  LED led_1 (.in(\функциональная_схема_мажоритарного_декодера_1_out_5 ));

  // Notes on the sheet:
  //   Мажоритарный кодек кода
  //   *
  //   *
  //   Исходные данные:
  //   m=4 
  //   d=8
  //   n=16
  //   r=11 
  //   tобн<= 7 
  //   tисп= 3 
  //   l=1 
  //   k=5 
  //   Савченко Е.А
  //   Савич О.А
  //   Матошко М.В
  //   s1
  //   Выполнили: ст. гр. 961401
  //   Выполнили: ст. гр. 961401
  //   Перминова А.В
endmodule

module \Функциональная_схема_кодера  (
  input  i1,
  input  i2,
  input  i3,
  input  i4,
  input  i5,
  output c1,
  output c2,
  output c3,
  output c4,
  output c5,
  output c6,
  output c7,
  output c8,
  output c9,
  output c10,
  output c11,
  output c12,
  output c13,
  output c14,
  output c15,
  output c16,
  output [15:0] out_22
);

  xor xor_1 (c2, i1, i5);
  xor xor_2 (c3, i1, i4);
  xor xor_3 (c4, i1, i4, i5);
  xor xor_4 (c5, i1, i3);
  xor xor_5 (c6, i1, i3, i5);
  xor xor_6 (c7, i1, i3, i4);
  xor xor_7 (c8, i1, i3, i4, i5);
  xor xor_8 (c9, i1, i2);
  xor xor_9 (c10, i1, i2, i5);
  xor xor_10 (c11, i1, i2, i4);
  xor xor_11 (c12, i1, i2, i4, i5);
  xor xor_12 (c13, i1, i2, i3);
  xor xor_13 (c14, i1, i2, i3, i5);
  xor xor_14 (c15, i1, i2, i3, i4);
  xor xor_15 (c16, i1, i2, i3, i4, i5);

  assign c1 = i1;
  assign out_22 = {i1, c2, c3, c4, c5, c6, c7, c8, c9, c10, c11, c12, c13, c14, c15, c16};
endmodule

module \Функциональная_схема_канала  (
  input  e1,
  input  e2,
  input  e3,
  input  e4,
  input  e5,
  input  e6,
  input  e7,
  input  e8,
  input  e9,
  input  e10,
  input  e11,
  input  e12,
  input  e13,
  input  e14,
  input  e15,
  input  e16,
  input  [15:0] in_17,
  output c1_star,
  output c2_star,
  output c3_star,
  output c4_star,
  output c5_star,
  output c6_star,
  output c7_star,
  output c8_star,
  output c9_star,
  output c10_star,
  output c11_star,
  output c12_star,
  output c13_star,
  output c14_star,
  output c15_star,
  output c16_star,
  output [15:0] out_34
);

  xor xor_1 (c1_star, e1, in_17[15]);
  xor xor_2 (c2_star, e2, in_17[14]);
  xor xor_3 (c3_star, e3, in_17[13]);
  xor xor_4 (c4_star, e4, in_17[12]);
  xor xor_5 (c5_star, e5, in_17[11]);
  xor xor_6 (c6_star, e6, in_17[10]);
  xor xor_7 (c7_star, e7, in_17[9]);
  xor xor_8 (c8_star, e8, in_17[8]);
  xor xor_9 (c9_star, e9, in_17[7]);
  xor xor_10 (c10_star, e10, in_17[6]);
  xor xor_11 (c11_star, e11, in_17[5]);
  xor xor_12 (c12_star, e12, in_17[4]);
  xor xor_13 (c13_star, e13, in_17[3]);
  xor xor_14 (c14_star, e14, in_17[2]);
  xor xor_15 (c15_star, e15, in_17[1]);
  xor xor_16 (c16_star, e16, in_17[0]);

  assign out_34 = {c1_star, c2_star, c3_star, c4_star, c5_star, c6_star, c7_star, c8_star, c9_star, c10_star, c11_star, c12_star, c13_star, c14_star, c15_star, c16_star};
endmodule

module \Функциональная_схема_мажоритарного_декодера  (
  input  [15:0] in_1,
  output out_2,
  output i1_star,
  output out_4,
  output out_5,
  output out_6,
  output out_7
);

  wire xor_1_out, xor_2_out, xor_3_out, xor_4_out, xor_5_out, xor_6_out, xor_7_out, xor_8_out, xor_9_out,
       xor_10_out, xor_11_out, xor_12_out, xor_13_out, xor_14_out, xor_15_out, xor_16_out, xor_17_out,
       xor_18_out, xor_19_out, xor_20_out, xor_21_out, xor_22_out, xor_23_out, xor_24_out, xor_25_out,
       xor_26_out, xor_27_out, xor_28_out, xor_29_out, xor_30_out, xor_31_out, xor_32_out, xor_33_out,
       xor_34_out, xor_35_out, xor_36_out, xor_37_out, xor_38_out, xor_39_out,
       \мажоритарный_элемент_на_восемь_входов_1_out_10 , \мажоритарный_элемент_на_восемь_входов_2_out_10 ,
       \мажоритарный_элемент_на_восемь_входов_3_out_10 , \мажоритарный_элемент_на_восемь_входов_4_out_10 ,
       \мажоритарный_элемент_на_восемь_входов_5_out_10 ;

  xor xor_1 (xor_1_out, in_1[7], in_1[15]);
  xor xor_2 (xor_2_out, in_1[6], in_1[14]);
  xor xor_3 (xor_3_out, in_1[5], in_1[13]);
  xor xor_4 (xor_4_out, in_1[4], in_1[12]);
  xor xor_5 (xor_5_out, in_1[3], in_1[11]);
  xor xor_6 (xor_6_out, in_1[2], in_1[10]);
  xor xor_7 (xor_7_out, in_1[1], in_1[9]);
  xor xor_8 (xor_8_out, in_1[0], in_1[8]);
  xor xor_9 (xor_9_out, in_1[11], in_1[15]);
  xor xor_10 (xor_10_out, in_1[10], in_1[14]);
  xor xor_11 (xor_11_out, in_1[9], in_1[13]);
  xor xor_12 (xor_12_out, in_1[8], in_1[12]);
  xor xor_13 (xor_13_out, in_1[3], in_1[7]);
  xor xor_14 (xor_14_out, in_1[2], in_1[6]);
  xor xor_15 (xor_15_out, in_1[1], in_1[5]);
  xor xor_16 (xor_16_out, in_1[0], in_1[4]);
  xor xor_17 (xor_17_out, in_1[13], in_1[15]);
  xor xor_18 (xor_18_out, in_1[12], in_1[14]);
  xor xor_19 (xor_19_out, in_1[9], in_1[11]);
  xor xor_20 (xor_20_out, in_1[8], in_1[10]);
  xor xor_21 (xor_21_out, in_1[5], in_1[7]);
  xor xor_22 (xor_22_out, in_1[4], in_1[6]);
  xor xor_23 (xor_23_out, in_1[1], in_1[3]);
  xor xor_24 (xor_24_out, in_1[0], in_1[2]);
  xor xor_25 (xor_25_out, in_1[14], in_1[15]);
  xor xor_26 (xor_26_out, in_1[12], in_1[13]);
  xor xor_27 (xor_27_out, in_1[10], in_1[11]);
  xor xor_28 (xor_28_out, in_1[8], in_1[9]);
  xor xor_29 (xor_29_out, in_1[6], in_1[7]);
  xor xor_30 (xor_30_out, in_1[4], in_1[5]);
  xor xor_31 (xor_31_out, in_1[2], in_1[3]);
  xor xor_32 (xor_32_out, in_1[0], in_1[1]);
  \Мажоритарный_элемент_на_восемь_входов  \u_мажоритарный_элемент_на_восемь_входов_1  (
    .in_1(xor_1_out), .in_2(xor_2_out), .in_3(xor_3_out), .in_4(xor_4_out), .in_5(xor_5_out),
    .in_6(xor_6_out), .in_7(xor_7_out), .in_8(xor_8_out), .out_9(out_2),
    .out_10(\мажоритарный_элемент_на_восемь_входов_1_out_10 ));
  \Мажоритарный_элемент_на_восемь_входов  \u_мажоритарный_элемент_на_восемь_входов_2  (
    .in_1(xor_9_out), .in_2(xor_10_out), .in_3(xor_11_out), .in_4(xor_12_out), .in_5(xor_13_out),
    .in_6(xor_14_out), .in_7(xor_15_out), .in_8(xor_16_out), .out_9(out_4),
    .out_10(\мажоритарный_элемент_на_восемь_входов_2_out_10 ));
  \Мажоритарный_элемент_на_восемь_входов  \u_мажоритарный_элемент_на_восемь_входов_3  (
    .in_1(xor_17_out), .in_2(xor_18_out), .in_3(xor_19_out), .in_4(xor_20_out), .in_5(xor_21_out),
    .in_6(xor_22_out), .in_7(xor_23_out), .in_8(xor_24_out), .out_9(out_6),
    .out_10(\мажоритарный_элемент_на_восемь_входов_3_out_10 ));
  \Мажоритарный_элемент_на_восемь_входов  \u_мажоритарный_элемент_на_восемь_входов_4  (
    .in_1(xor_25_out), .in_2(xor_26_out), .in_3(xor_27_out), .in_4(xor_28_out), .in_5(xor_29_out),
    .in_6(xor_30_out), .in_7(xor_31_out), .in_8(xor_32_out), .out_9(out_7),
    .out_10(\мажоритарный_элемент_на_восемь_входов_4_out_10 ));
  xor xor_33 (xor_33_out, out_2, in_1[7]);
  xor xor_34 (xor_34_out, in_1[11], out_4);
  xor xor_35 (xor_35_out, out_4, out_6, in_1[9]);
  xor xor_36 (xor_36_out, out_4, out_7, in_1[10]);
  xor xor_37 (xor_37_out, out_6, in_1[13]);
  xor xor_38 (xor_38_out, out_6, out_7, in_1[12]);
  xor xor_39 (xor_39_out, out_7, in_1[14]);
  \Мажоритарный_элемент_на_восемь_входов  \u_мажоритарный_элемент_на_восемь_входов_5  (
    .in_1(in_1[0]), .in_2(xor_33_out), .in_3(xor_35_out), .in_4(xor_36_out), .in_5(xor_34_out),
    .in_6(xor_38_out), .in_7(xor_37_out), .in_8(xor_39_out), .out_9(i1_star),
    .out_10(\мажоритарный_элемент_на_восемь_входов_5_out_10 ));
  or or_1 (out_5, \мажоритарный_элемент_на_восемь_входов_1_out_10 , \мажоритарный_элемент_на_восемь_входов_2_out_10 , \мажоритарный_элемент_на_восемь_входов_3_out_10 , \мажоритарный_элемент_на_восемь_входов_4_out_10 , \мажоритарный_элемент_на_восемь_входов_5_out_10 );

  // Notes on the sheet:
  //   i2*
  //   i3*
  //   i4*
  //   i5*
endmodule

module \Мажоритарный_элемент_на_восемь_входов  (
  input  in_1,
  input  in_2,
  input  in_3,
  input  in_4,
  input  in_5,
  input  in_6,
  input  in_7,
  input  in_8,
  output out_9,
  output out_10
);

  wire [3:0] bitadder_1_out;

  BitAdder #(.width(1)) bitadder_1 (
    .in0(in_1), .in1(in_2), .in2(in_3), .in3(in_4), .in4(in_5), .in5(in_6), .in6(in_7), .in7(in_8),
    .out(bitadder_1_out));
  Comparator #(.width(4), .mode("unsigned")) comparator_1 (
    .a(bitadder_1_out), .b(4'b0100), .gt(out_9), .eq(out_10));  // open: lt
endmodule
