// Logisim project pz7_ptk.circ as structural Verilog: 4 circuits, main circuit Структурная схема кодека
module \Структурная_схема_кодека  (
  input  i1,
  input  e1,
  input  i2,
  input  e2,
  input  i3,
  input  e3,
  input  i4,
  input  e4,
  input  i5,
  input  e5,
  input  i6,
  input  e6,
  input  i7,
  input  e7,
  input  i8,
  input  e8,
  input  i9,
  input  e9,
  input  e10,
  input  e11,
  input  e12,
  input  e13,
  input  e14,
  input  e15,
  output \с1 ,
  output e1_star,
  output i1_star,
  output \с2 ,
  output e2_star,
  output i2_star,
  output \с3 ,
  output e3_star,
  output i3_star,
  output \с4 ,
  output e4_star,
  output i4_star,
  output \с5 ,
  output e5_star,
  output i5_star,
  output \с6 ,
  output e6_star,
  output i6_star,
  output \с7 ,
  output e7_star,
  output i7_star,
  output \с8 ,
  output e8_star,
  output i8_star,
  output \с9 ,
  output e9_star,
  output i9_star,
  output \с10 ,
  output e10_star,
  output \с11 ,
  output e11_star,
  output \с12 ,
  output e12_star,
  output \с13 ,
  output e13_star,
  output \с14 ,
  output e14_star,
  output \с15 ,
  output e15_star
);

  wire [14:0] \функциональная_схема_канала_1_out_32 , \функциональная_схема_кодера_1_out_25 ;

  \Функциональная_схема_кодера  \u_функциональная_схема_кодера_1  (
    .i1(i1), .i2(i2), .i3(i3), .i4(i4), .i5(i5), .i6(i6), .i7(i7), .i8(i8), .i9(i9),
    .out_25(\функциональная_схема_кодера_1_out_25 ), .c1(\с1 ), .c2(\с2 ), .c3(\с3 ), .c4(\с4 ), .c5(\с5 ),
    .c6(\с6 ), .c7(\с7 ), .c8(\с8 ), .c9(\с9 ), .c10(\с10 ), .c11(\с11 ), .c12(\с12 ), .c13(\с13 ),
    .c14(\с14 ), .c15(\с15 ));
  \Функциональная_схема_канала  \u_функциональная_схема_канала_1  (
    .e1(e1), .e2(e2), .e3(e3), .e4(e4), .e5(e5), .e6(e6), .e7(e7), .e8(e8), .e9(e9), .e10(e10), .e11(e11),
    .e12(e12), .e13(e13), .e14(e14), .e15(e15), .in_16(\функциональная_схема_кодера_1_out_25 ),
    .\с1_star (e1_star), .\с2_star (e2_star), .\с3_star (e3_star), .\с4_star (e4_star), .\с5_star (e5_star),
    .\с6_star (e6_star), .\с7_star (e7_star), .\с8_star (e8_star), .\с9_star (e9_star),
    .\с10_star (e10_star), .\с11_star (e11_star), .\с12_star (e12_star), .\с13_star (e13_star),
    .\с14_star (e14_star), .\с15_star (e15_star), .out_32(\функциональная_схема_канала_1_out_32 ));
  \Функциональная_схема_декодера  \u_функциональная_схема_декодера_1  (
    .i1_star(i1_star), .i2_star(i2_star), .i3_star(i3_star), .i4_star(i4_star), .i5_star(i5_star),
    .i6_star(i6_star), .i7_star(i7_star), .i8_star(i8_star), .i9_star(i9_star),
    .in_1(\функциональная_схема_канала_1_out_32 ));

  // Notes on the sheet:
  //   Кодер
  //   Кодек итеративного кода
  //   Канал
  //   Декодер
endmodule

module \Функциональная_схема_кодера  (
  input  i1,
  input  i2,
  input  i3,
  input  i4,
  input  i5,
  input  i6,
  input  i7,
  input  i8,
  input  i9,
  output c1,
  output c2,
  output c3,
  output c4,
  output c5,
  output c6,
  output c7,
  output c8,
  output c9,
  output c10,
  output c11,
  output c12,
  output c13,
  output c14,
  output c15,
  output [14:0] out_25
);

  xor xor_1 (c6, i7, i8, i9);
  xor xor_2 (c10, i4, i5, i6);
  xor xor_3 (c12, i1, i2, i3);
  xor xor_4 (c13, i1, i4, i7);
  xor xor_5 (c14, i2, i5, i8);
  xor xor_6 (c15, i3, i6, i9);

  assign c1 = i1;
  assign c2 = i5;
  assign c3 = i9;
  assign c4 = i2;
  assign c5 = i6;
  assign c7 = i4;
  assign c8 = i8;
  assign c9 = i3;
  assign c11 = i7;
  assign out_25 = {i1, i5, i9, i2, i6, c6, i4, i8, i3, c10, i7, c12, c13, c14, c15};
endmodule

module \Функциональная_схема_канала  (
  input  e1,
  input  e2,
  input  e3,
  input  e4,
  input  e5,
  input  e6,
  input  e7,
  input  e8,
  input  e9,
  input  e10,
  input  e11,
  input  e12,
  input  e13,
  input  e14,
  input  e15,
  input  [14:0] in_16,
  output \с1_star ,
  output \с2_star ,
  output \с3_star ,
  output \с4_star ,
  output \с5_star ,
  output \с6_star ,
  output \с7_star ,
  output \с8_star ,
  output \с9_star ,
  output \с10_star ,
  output \с11_star ,
  output \с12_star ,
  output \с13_star ,
  output \с14_star ,
  output \с15_star ,
  output [14:0] out_32
);

  xor xor_1 (out_32[0], e1, in_16[14]);
  xor xor_2 (out_32[1], e2, in_16[13]);
  xor xor_3 (out_32[2], e3, in_16[12]);
  xor xor_4 (out_32[3], e4, in_16[11]);
  xor xor_5 (out_32[4], e5, in_16[10]);
  xor xor_6 (out_32[5], e6, in_16[9]);
  xor xor_7 (out_32[6], e7, in_16[8]);
  xor xor_8 (out_32[7], e8, in_16[7]);
  xor xor_9 (out_32[8], e9, in_16[6]);
  xor xor_10 (out_32[9], e10, in_16[5]);
  xor xor_11 (out_32[10], e11, in_16[4]);
  xor xor_12 (out_32[11], e12, in_16[3]);
  xor xor_13 (out_32[12], e13, in_16[2]);
  xor xor_14 (out_32[13], e14, in_16[1]);
  xor xor_15 (out_32[14], e15, in_16[0]);

  assign \с1_star  = out_32[0];
  assign \с2_star  = out_32[1];
  assign \с3_star  = out_32[2];
  assign \с4_star  = out_32[3];
  assign \с5_star  = out_32[4];
  assign \с6_star  = out_32[5];
  assign \с7_star  = out_32[6];
  assign \с8_star  = out_32[7];
  assign \с9_star  = out_32[8];
  assign \с10_star  = out_32[9];
  assign \с11_star  = out_32[10];
  assign \с12_star  = out_32[11];
  assign \с13_star  = out_32[12];
  assign \с14_star  = out_32[13];
  assign \с15_star  = out_32[14];
endmodule

module \Функциональная_схема_декодера  (
  input  [14:0] in_1,
  output i1_star,
  output i2_star,
  output i3_star,
  output i4_star,
  output i5_star,
  output i6_star,
  output i7_star,
  output i8_star,
  output i9_star
);

  wire and_1_out, and_2_out, and_3_out, and_4_out, and_5_out, and_6_out, and_7_out, and_8_out, and_9_out,
       r1_star_out, r2_star_out, r3_star_out, r4_star_out, r5_star_out, r6_star_out, xor_1_out, xor_2_out,
       xor_3_out, xor_4_out, xor_5_out, xor_6_out;

  xor r1_star (r1_star_out, in_1[0], in_1[3], in_1[8]);
  xor r2_star (r2_star_out, in_1[1], in_1[4], in_1[6]);
  xor r3_star (r3_star_out, in_1[2], in_1[7], in_1[10]);
  xor r4_star (r4_star_out, in_1[0], in_1[6], in_1[10]);
  xor r5_star (r5_star_out, in_1[1], in_1[3], in_1[7]);
  xor r6_star (r6_star_out, in_1[2], in_1[4], in_1[8]);
  and and_1 (and_1_out, xor_1_out, xor_4_out);
  xor xor_1 (xor_1_out, in_1[11], r1_star_out);
  xor xor_2 (xor_2_out, in_1[9], r2_star_out);
  xor xor_3 (xor_3_out, in_1[5], r3_star_out);
  xor xor_4 (xor_4_out, in_1[12], r4_star_out);
  xor xor_5 (xor_5_out, in_1[13], r5_star_out);
  xor xor_6 (xor_6_out, in_1[14], r6_star_out);
  and and_2 (and_2_out, xor_1_out, xor_5_out);
  and and_3 (and_3_out, xor_1_out, xor_6_out);
  and and_4 (and_4_out, xor_2_out, xor_4_out);
  and and_5 (and_5_out, xor_2_out, xor_5_out);
  and and_6 (and_6_out, xor_2_out, xor_6_out);
  and and_7 (and_7_out, xor_3_out, xor_4_out);
  and and_8 (and_8_out, xor_3_out, xor_6_out);
  and and_9 (and_9_out, xor_3_out, xor_5_out);
  xor xor_7 (i1_star, in_1[0], and_1_out);
  xor xor_8 (i2_star, in_1[3], and_2_out);
  xor xor_9 (i3_star, in_1[8], and_3_out);
  xor xor_10 (i4_star, in_1[6], and_4_out);
  xor xor_11 (i5_star, in_1[1], and_5_out);
  xor xor_12 (i6_star, in_1[4], and_6_out);
  xor xor_13 (i7_star, in_1[10], and_7_out);
  xor xor_14 (i8_star, in_1[7], and_9_out);
  xor xor_15 (i9_star, in_1[2], and_8_out);
endmodule
