// Logisim project pz8_ptk.circ as structural Verilog: 6 circuits, main circuit Структурная схема
module \Структурная_схема  (
  input  in_1,
  input  in_2,
  input  in_3,
  input  in_4,
  input  in_5,
  input  in_6,
  input  in_7,
  input  in_8,
  input  in_9,
  input  in_10,
  input  in_11,
  input  in_12,
  input  in_13,
  input  in_14,
  input  in_15,
  input  in_16,
  input  in_17,
  input  in_18,
  input  in_19,
  input  in_20,
  input  in_21,
  input  in_22,
  input  in_23,
  input  in_24,
  input  in_25,
  input  in_26,
  input  in_27,
  input  in_28,
  input  in_29,
  input  in_30,
  input  in_31,
  input  in_32,
  input  in_33,
  output out_34,
  output out_35,
  output out_36,
  output out_37,
  output out_38,
  output out_39,
  output out_40,
  output out_41,
  output out_42,
  output out_43,
  output out_44,
  output out_45,
  output out_46,
  output out_47,
  output out_48,
  output out_49,
  output out_50,
  output out_51,
  output out_52,
  output out_53,
  output out_54,
  output out_55,
  output out_56,
  output out_57,
  output out_58,
  output out_59,
  output out_60,
  output out_61,
  output out_62,
  output out_63,
  output out_64,
  output out_65,
  output out_66,
  output out_67,
  output out_68,
  output out_69,
  output out_70,
  output out_71,
  output out_72,
  output out_73,
  output out_74,
  output out_75,
  output out_76,
  output out_77,
  output out_78,
  output out_79,
  output out_80,
  output out_81,
  output out_82,
  output out_83,
  output out_84,
  output out_85,
  output out_86,
  output out_87
);

  wire \функциональная_схема_кодера_1_c1 , \функциональная_схема_кодера_1_c2 ,
       \функциональная_схема_кодера_1_c3 , \функциональная_схема_кодера_1_c4 ,
       \функциональная_схема_кодера_1_c5 , \функциональная_схема_кодера_1_c6 ,
       \функциональная_схема_кодера_1_c7 , \функциональная_схема_кодера_2_c1 ,
       \функциональная_схема_кодера_2_c2 , \функциональная_схема_кодера_2_c3 ,
       \функциональная_схема_кодера_2_c4 , \функциональная_схема_кодера_2_c5 ,
       \функциональная_схема_кодера_2_c6 , \функциональная_схема_кодера_2_c7 ,
       \функциональная_схема_кодера_3_c1 , \функциональная_схема_кодера_3_c2 ,
       \функциональная_схема_кодера_3_c3 , \функциональная_схема_кодера_3_c4 ,
       \функциональная_схема_кодера_3_c5 , \функциональная_схема_кодера_3_c6 ,
       \функциональная_схема_кодера_3_c7 ;
  wire [6:0] \функциональная_схема_деперемежителя_1_out_2 , \функциональная_схема_деперемежителя_1_out_3 ,
       \функциональная_схема_деперемежителя_1_out_4 ;
  wire [20:0] \функциональная_схема_канала_1_out_44 , \функциональная_схема_перемежителя_1_out_43 ;

  \Функциональная_схема_кодера  \u_функциональная_схема_кодера_1  (
    .i1(in_1), .i2(in_2), .i3(in_4), .i4(in_6), .c1(\функциональная_схема_кодера_1_c1 ),
    .c2(\функциональная_схема_кодера_1_c2 ), .c3(\функциональная_схема_кодера_1_c3 ),
    .c4(\функциональная_схема_кодера_1_c4 ), .c5(\функциональная_схема_кодера_1_c5 ),
    .c6(\функциональная_схема_кодера_1_c6 ), .c7(\функциональная_схема_кодера_1_c7 ));
  \Функциональная_схема_кодера  \u_функциональная_схема_кодера_2  (
    .i1(in_13), .i2(in_15), .i3(in_17), .i4(in_19), .c1(\функциональная_схема_кодера_2_c1 ),
    .c2(\функциональная_схема_кодера_2_c2 ), .c3(\функциональная_схема_кодера_2_c3 ),
    .c4(\функциональная_схема_кодера_2_c4 ), .c5(\функциональная_схема_кодера_2_c5 ),
    .c6(\функциональная_схема_кодера_2_c6 ), .c7(\функциональная_схема_кодера_2_c7 ));
  \Функциональная_схема_кодера  \u_функциональная_схема_кодера_3  (
    .i1(in_25), .i2(in_27), .i3(in_29), .i4(in_31), .c1(\функциональная_схема_кодера_3_c1 ),
    .c2(\функциональная_схема_кодера_3_c2 ), .c3(\функциональная_схема_кодера_3_c3 ),
    .c4(\функциональная_схема_кодера_3_c4 ), .c5(\функциональная_схема_кодера_3_c5 ),
    .c6(\функциональная_схема_кодера_3_c6 ), .c7(\функциональная_схема_кодера_3_c7 ));
  \Функциональная_схема_перемежителя  \u_функциональная_схема_перемежителя_1  (
    .out_22(out_35), .out_23(out_38), .out_24(out_41), .out_25(out_44), .out_26(out_46), .out_27(out_48),
    .out_28(out_50), .out_29(out_53), .out_30(out_56), .out_31(out_59), .out_32(out_62), .out_33(out_64),
    .out_34(out_66), .out_35(out_68), .out_36(out_71), .out_37(out_74), .out_38(out_77), .out_39(out_80),
    .out_40(out_82), .out_41(out_84), .out_42(out_86), .out_43(\функциональная_схема_перемежителя_1_out_43 ),
    .in_1(\функциональная_схема_кодера_1_c1 ), .in_2(\функциональная_схема_кодера_1_c2 ),
    .in_3(\функциональная_схема_кодера_1_c3 ), .in_4(\функциональная_схема_кодера_1_c4 ),
    .in_5(\функциональная_схема_кодера_1_c5 ), .in_6(\функциональная_схема_кодера_1_c6 ),
    .in_7(\функциональная_схема_кодера_1_c7 ), .in_8(\функциональная_схема_кодера_2_c1 ),
    .in_9(\функциональная_схема_кодера_2_c2 ), .in_10(\функциональная_схема_кодера_2_c3 ),
    .in_11(\функциональная_схема_кодера_2_c4 ), .in_12(\функциональная_схема_кодера_2_c5 ),
    .in_13(\функциональная_схема_кодера_2_c6 ), .in_14(\функциональная_схема_кодера_2_c7 ),
    .in_15(\функциональная_схема_кодера_3_c1 ), .in_16(\функциональная_схема_кодера_3_c2 ),
    .in_17(\функциональная_схема_кодера_3_c3 ), .in_18(\функциональная_схема_кодера_3_c4 ),
    .in_19(\функциональная_схема_кодера_3_c5 ), .in_20(\функциональная_схема_кодера_3_c6 ),
    .in_21(\функциональная_схема_кодера_3_c7 ));
  \Функциональная_схема_канала  \u_функциональная_схема_канала_1  (
    .in_1(in_3), .in_2(in_5), .in_3(in_7), .in_4(in_8), .in_5(in_9), .in_6(in_10), .in_7(in_11),
    .in_8(in_12), .in_9(in_14), .in_10(in_16), .in_11(in_18), .in_12(in_20), .in_13(in_21), .in_14(in_22),
    .in_15(in_23), .in_16(in_24), .in_17(in_26), .in_18(in_28), .in_19(in_30), .in_20(in_32), .in_21(in_33),
    .in_22(\функциональная_схема_перемежителя_1_out_43 ), .out_23(out_36), .out_24(out_39), .out_25(out_42),
    .out_26(out_45), .out_27(out_47), .out_28(out_49), .out_29(out_51), .out_30(out_54), .out_31(out_57),
    .out_32(out_60), .out_33(out_63), .out_34(out_65), .out_35(out_67), .out_36(out_69), .out_37(out_72),
    .out_38(out_75), .out_39(out_78), .out_40(out_81), .out_41(out_83), .out_42(out_85), .out_43(out_87),
    .out_44(\функциональная_схема_канала_1_out_44 ));
  \Функциональная_схема_деперемежителя  \u_функциональная_схема_деперемежителя_1  (
    .out_2(\функциональная_схема_деперемежителя_1_out_2 ),
    .out_3(\функциональная_схема_деперемежителя_1_out_3 ),
    .out_4(\функциональная_схема_деперемежителя_1_out_4 ), .in_1(\функциональная_схема_канала_1_out_44 ));
  \Функциональная_схеа_декодера  \u_функциональная_схеа_декодера_1  (
    .in_1(\функциональная_схема_деперемежителя_1_out_2 ), .i1_star(out_34), .i2_star(out_37),
    .i3_star(out_40), .i4_star(out_43));
  \Функциональная_схеа_декодера  \u_функциональная_схеа_декодера_2  (
    .in_1(\функциональная_схема_деперемежителя_1_out_3 ), .i1_star(out_52), .i2_star(out_55),
    .i3_star(out_58), .i4_star(out_61));
  \Функциональная_схеа_декодера  \u_функциональная_схеа_декодера_3  (
    .in_1(\функциональная_схема_деперемежителя_1_out_4 ), .i1_star(out_70), .i2_star(out_73),
    .i3_star(out_76), .i4_star(out_79));

  // Notes on the sheet:
  //   Кодер
  //   Канал
  //   Декодер
endmodule

module \Функциональная_схема_кодера  (
  input  i1,
  input  i2,
  input  i3,
  input  i4,
  output c1,
  output c2,
  output c3,
  output c4,
  output c5,
  output c6,
  output c7
);

  xor xor_1 (c5, i1, i2, i4);
  xor xor_2 (c6, i1, i3, i4);
  xor xor_3 (c7, i2, i3, i4);

  assign c1 = i1;
  assign c2 = i2;
  assign c3 = i3;
  assign c4 = i4;
endmodule

module \Функциональная_схема_канала  (
  input  in_1,
  input  in_2,
  input  in_3,
  input  in_4,
  input  in_5,
  input  in_6,
  input  in_7,
  input  in_8,
  input  in_9,
  input  in_10,
  input  in_11,
  input  in_12,
  input  in_13,
  input  in_14,
  input  in_15,
  input  in_16,
  input  in_17,
  input  in_18,
  input  in_19,
  input  in_20,
  input  in_21,
  input  [20:0] in_22,
  output out_23,
  output out_24,
  output out_25,
  output out_26,
  output out_27,
  output out_28,
  output out_29,
  output out_30,
  output out_31,
  output out_32,
  output out_33,
  output out_34,
  output out_35,
  output out_36,
  output out_37,
  output out_38,
  output out_39,
  output out_40,
  output out_41,
  output out_42,
  output out_43,
  output [20:0] out_44
);

  xor xor_1 (out_23, in_1, in_22[20]);
  xor xor_2 (out_24, in_2, in_22[19]);
  xor xor_3 (out_25, in_3, in_22[18]);
  xor xor_4 (out_26, in_4, in_22[17]);
  xor xor_5 (out_27, in_5, in_22[16]);
  xor xor_6 (out_28, in_6, in_22[15]);
  xor xor_7 (out_29, in_7, in_22[14]);
  xor xor_8 (out_30, in_8, in_22[13]);
  xor xor_9 (out_31, in_9, in_22[12]);
  xor xor_10 (out_32, in_10, in_22[11]);
  xor xor_11 (out_33, in_11, in_22[10]);
  xor xor_12 (out_34, in_12, in_22[9]);
  xor xor_13 (out_35, in_13, in_22[8]);
  xor xor_14 (out_36, in_14, in_22[7]);
  xor xor_15 (out_37, in_15, in_22[6]);
  xor xor_16 (out_38, in_16, in_22[5]);
  xor xor_17 (out_39, in_17, in_22[4]);
  xor xor_18 (out_40, in_18, in_22[3]);
  xor xor_19 (out_41, in_19, in_22[2]);
  xor xor_20 (out_42, in_20, in_22[1]);
  xor xor_21 (out_43, in_21, in_22[0]);

  assign out_44 = {out_23, out_24, out_25, out_26, out_27, out_28, out_29, out_30, out_31, out_32, out_33, out_34, out_35, out_36, out_37, out_38, out_39, out_40, out_41, out_42, out_43};
endmodule

module \Функциональная_схеа_декодера  (
  input  [6:0] in_1,
  output i1_star,
  output i2_star,
  output i3_star,
  output i4_star
);

  wire and_1_out, and_2_out, and_3_out, and_4_out, not_1_out, not_2_out, not_3_out, xor_1_out, xor_2_out,
       xor_3_out;

  xor xor_1 (xor_1_out, in_1[6], in_1[5], in_1[3], in_1[2]);
  xor xor_2 (xor_2_out, in_1[6], in_1[4], in_1[3], in_1[1]);
  xor xor_3 (xor_3_out, in_1[5], in_1[4], in_1[3], in_1[0]);
  not not_1 (not_1_out, xor_3_out);
  not not_2 (not_2_out, xor_2_out);
  not not_3 (not_3_out, xor_1_out);
  and and_1 (and_1_out, xor_1_out, xor_2_out, not_1_out);
  and and_2 (and_2_out, xor_1_out, not_2_out, xor_3_out);
  and and_3 (and_3_out, not_3_out, xor_2_out, xor_3_out);
  and and_4 (and_4_out, xor_1_out, xor_2_out, xor_3_out);
  xor xor_4 (i1_star, in_1[6], and_1_out);
  xor xor_5 (i2_star, in_1[5], and_2_out);
  xor xor_6 (i3_star, in_1[4], and_3_out);
  xor xor_7 (i4_star, in_1[3], and_4_out);
endmodule

module \Функциональная_схема_перемежителя  (
  input  in_1,
  input  in_2,
  input  in_3,
  input  in_4,
  input  in_5,
  input  in_6,
  input  in_7,
  input  in_8,
  input  in_9,
  input  in_10,
  input  in_11,
  input  in_12,
  input  in_13,
  input  in_14,
  input  in_15,
  input  in_16,
  input  in_17,
  input  in_18,
  input  in_19,
  input  in_20,
  input  in_21,
  output out_22,
  output out_23,
  output out_24,
  output out_25,
  output out_26,
  output out_27,
  output out_28,
  output out_29,
  output out_30,
  output out_31,
  output out_32,
  output out_33,
  output out_34,
  output out_35,
  output out_36,
  output out_37,
  output out_38,
  output out_39,
  output out_40,
  output out_41,
  output out_42,
  output [20:0] out_43
);


  assign out_22 = in_1;
  assign out_23 = in_8;
  assign out_24 = in_15;
  assign out_25 = in_2;
  assign out_26 = in_9;
  assign out_27 = in_16;
  assign out_28 = in_3;
  assign out_29 = in_10;
  assign out_30 = in_17;
  assign out_31 = in_4;
  assign out_32 = in_11;
  assign out_33 = in_18;
  assign out_34 = in_5;
  assign out_35 = in_12;
  assign out_36 = in_19;
  assign out_37 = in_6;
  assign out_38 = in_13;
  assign out_39 = in_20;
  assign out_40 = in_7;
  assign out_41 = in_14;
  assign out_42 = in_21;
  assign out_43 = {in_1, in_8, in_15, in_2, in_9, in_16, in_3, in_10, in_17, in_4, in_11, in_18, in_5, in_12, in_19, in_6, in_13, in_20, in_7, in_14, in_21};
endmodule

module \Функциональная_схема_деперемежителя  (
  input  [20:0] in_1,
  output [6:0] out_2,
  output [6:0] out_3,
  output [6:0] out_4
);


  assign out_2 = {in_1[20], in_1[17], in_1[14], in_1[11], in_1[8], in_1[5], in_1[2]};
  assign out_3 = {in_1[19], in_1[16], in_1[13], in_1[10], in_1[7], in_1[4], in_1[1]};
  assign out_4 = {in_1[18], in_1[15], in_1[12], in_1[9], in_1[6], in_1[3], in_1[0]};
endmodule
