// Logisim project Savchenko961401.circ as structural Verilog: 15 circuits, main circuit Кодек - Структурная схема
module \Кодек___Структурная_схема  (
  input  \Старт ,
  input  \Старт_2 ,
  input  \Старт_3 
);

  wire rom_1_data, rom_2_data, \декодер_функциональная_схема_1_выход ,
       \декодер_функциональная_схема_1_индикатор_окончания_работы_декодера ,
       \декодер_функциональная_схема_1_очистка_озу , \декодер_функциональная_схема_1_такты_для_озу ,
       \канал_функциональная_схема_1_данные_для_записи_в_буфер_декодера ,
       \канал_функциональная_схема_1_индикатор_окончания_работы_канала ,
       \канал_функциональная_схема_1_кодовое_слово_с_ошибками ,
       \канал_функциональная_схема_1_очистка_озу_канала ,
       \канал_функциональная_схема_1_такты_для_буфера_декодера ,
       \канал_функциональная_схема_1_такты_для_озу_канала ,
       \канал_функциональная_схема_1_управление_буфером_декодера ,
       \кодер_функциональная_схема_1_данные_для_записи_в_буфер_канала ,
       \кодер_функциональная_схема_1_данные_для_записи_в_озу_кодера ,
       \кодер_функциональная_схема_1_индикатор_окончания_работы_кодера ,
       \кодер_функциональная_схема_1_очистка_озу_кодера ,
       \кодер_функциональная_схема_1_такты_для_буфера_канала ,
       \кодер_функциональная_схема_1_такты_для_озу_кодера ,
       \кодер_функциональная_схема_1_управление_буфером_канала ;
  wire [6:0] \декодер_функциональная_схема_1_шина_адреса_озу ,
       \канал_функциональная_схема_1_шина_адреса_буфера_декодера ,
       \канал_функциональная_схема_1_шина_адреса_озу_канала ,
       \канал_функциональная_схема_1_шина_адреса_пзу_канала ,
       \кодер_функциональная_схема_1_шина_адреса_буфера_канала ,
       \кодер_функциональная_схема_1_шина_адреса_озу_кодера ,
       \кодер_функциональная_схема_1_шина_адреса_пзу_кодера ;

  LED led_1 (.in(\кодер_функциональная_схема_1_индикатор_окончания_работы_кодера ));
  LED led_2 (.in(\декодер_функциональная_схема_1_индикатор_окончания_работы_декодера ));
  ROM #(.addrWidth(7), .dataWidth(1)) rom_1 (
    .addr(\кодер_функциональная_схема_1_шина_адреса_пзу_кодера ), .data(rom_1_data));  // open: sel
  RAM #(.addrWidth(7), .dataWidth(1), .bus("separate")) ram_1 (
    .addr(\декодер_функциональная_схема_1_шина_адреса_озу ), .din(\декодер_функциональная_схема_1_выход ),
    .clk(\декодер_функциональная_схема_1_такты_для_озу ), .clr(\декодер_функциональная_схема_1_очистка_озу ));  // open: data, str, sel, ld
  RAM #(.addrWidth(7), .dataWidth(1), .bus("separate")) ram_2 (
    .addr(\кодер_функциональная_схема_1_шина_адреса_озу_кодера ),
    .din(\кодер_функциональная_схема_1_данные_для_записи_в_озу_кодера ),
    .clk(\кодер_функциональная_схема_1_такты_для_озу_кодера ),
    .clr(\кодер_функциональная_схема_1_очистка_озу_кодера ));  // open: data, str, sel, ld
  \Кодер___Функциональная_схема  \u_кодер_функциональная_схема_1  (
    .\Старт (\Старт ),
    .\Индикатор_окончания_работы_кодера (\кодер_функциональная_схема_1_индикатор_окончания_работы_кодера ),
    .\Данные_для_записи_в_ОЗУ_кодера (\кодер_функциональная_схема_1_данные_для_записи_в_озу_кодера ),
    .\Такты_для_ОЗУ_кодера (\кодер_функциональная_схема_1_такты_для_озу_кодера ), .\Вход (rom_1_data),
    .\Шина_адреса_ОЗУ_кодера (\кодер_функциональная_схема_1_шина_адреса_озу_кодера ),
    .\Очистка_ОЗУ_кодера (\кодер_функциональная_схема_1_очистка_озу_кодера ),
    .\Шина_адреса_ПЗУ_кодера (\кодер_функциональная_схема_1_шина_адреса_пзу_кодера ),
    .\Шина_адреса_буфера_канала (\кодер_функциональная_схема_1_шина_адреса_буфера_канала ),
    .\Такты_для_буфера_канала (\кодер_функциональная_схема_1_такты_для_буфера_канала ),
    .\Данные_для_записи_в_буфер_канала (\кодер_функциональная_схема_1_данные_для_записи_в_буфер_канала ),
    .\Управление_буфером_канала (\кодер_функциональная_схема_1_управление_буфером_канала ));
  \Декодер___Функциональная_схема  \u_декодер_функциональная_схема_1  (
    .\Такты_для_ОЗУ (\декодер_функциональная_схема_1_такты_для_озу ),
    .\Шина_адреса_ОЗУ (\декодер_функциональная_схема_1_шина_адреса_озу ), .\Старт (\Старт_3 ),
    .\Индикатор_окончания_работы_декодера (\декодер_функциональная_схема_1_индикатор_окончания_работы_декодера ),
    .\Очистка_ОЗУ (\декодер_функциональная_схема_1_очистка_озу ),
    .\Выход (\декодер_функциональная_схема_1_выход ),
    .\Управление_буфером (\канал_функциональная_схема_1_управление_буфером_декодера ),
    .\Шина_адреса_буфера (\канал_функциональная_схема_1_шина_адреса_буфера_декодера ),
    .\Такты_канала (\канал_функциональная_схема_1_такты_для_буфера_декодера ),
    .\Вход (\канал_функциональная_схема_1_данные_для_записи_в_буфер_декодера ));
  \Канал___Функциональная_схема  \u_канал_функциональная_схема_1  (
    .\Старт (\Старт_2 ),
    .\Кодовое_слово_с_ошибками (\канал_функциональная_схема_1_кодовое_слово_с_ошибками ),
    .\Индикатор_окончания_работы_канала (\канал_функциональная_схема_1_индикатор_окончания_работы_канала ),
    .\Такты_для_ОЗУ_канала (\канал_функциональная_схема_1_такты_для_озу_канала ),
    .\Шина_адреса_буфера_декодера (\канал_функциональная_схема_1_шина_адреса_буфера_декодера ),
    .\Шина_адреса_ПЗУ_канала (\канал_функциональная_схема_1_шина_адреса_пзу_канала ),
    .\Очистка_ОЗУ_канала (\канал_функциональная_схема_1_очистка_озу_канала ), .\Ошибки (rom_2_data),
    .\Шина_адреса_буфера_канала (\кодер_функциональная_схема_1_шина_адреса_буфера_канала ),
    .\Вход (\кодер_функциональная_схема_1_данные_для_записи_в_буфер_канала ),
    .\Такты_кодера (\кодер_функциональная_схема_1_такты_для_буфера_канала ),
    .\Управление_буфером_канала (\кодер_функциональная_схема_1_управление_буфером_канала ),
    .\Управление_буфером_декодера (\канал_функциональная_схема_1_управление_буфером_декодера ),
    .\Шина_адреса_ОЗУ_канала (\канал_функциональная_схема_1_шина_адреса_озу_канала ),
    .\Такты_для_буфера_декодера (\канал_функциональная_схема_1_такты_для_буфера_декодера ),
    .\Данные_для_записи_в_буфер_декодера (\канал_функциональная_схема_1_данные_для_записи_в_буфер_декодера ));
  ROM #(.addrWidth(7), .dataWidth(1)) rom_2 (
    .addr(\канал_функциональная_схема_1_шина_адреса_пзу_канала ), .data(rom_2_data));  // open: sel
  RAM #(.addrWidth(7), .dataWidth(1), .bus("separate")) ram_3 (
    .addr(\канал_функциональная_схема_1_шина_адреса_озу_канала ),
    .din(\канал_функциональная_схема_1_кодовое_слово_с_ошибками ),
    .clk(\канал_функциональная_схема_1_такты_для_озу_канала ),
    .clr(\канал_функциональная_схема_1_очистка_озу_канала ));  // open: data, str, sel, ld
  LED led_3 (.in(\канал_функциональная_схема_1_индикатор_окончания_работы_канала ));

  // Notes on the sheet:
  //   Кодек Файра
  //   p(x)=x^4+x+1 неприводимый многочлен
  //   3. Задать информационный вектор
  //   7. Подождать 105 такт работы канала
  //   b=4 длина исправляемого пакета ошибок
  //   m>=b=4 степень неприводимого многчлена
  //   с>=2*b-1=7 степень двучлена x^c+1; x^7+1
  //   n = НОК(с; 2^m-1) = НОК(7; 15) = 105  - длина кода
  //   r = с + m = 7 + 4 = 11 -  количество проверочных разрядов
  //   2. Выбрать пункт "Такты включены" в меню "Моделировать"
  //   9. Подождать 210 такта работы декодера
  //   Информация
  //   Информация*
  //   k = n - r = 105 - 11 = 94  - количество информационных разрядов
  //   Запуск кодека
  //   1. Выбрать пункт "8 Гц" в меню "Моделировать\Тактовая частота"
  //   4. Переключить "Старт" кодера в значение "1" и сразу в значение "0"
  //   5. Подождать 105 такт работы кодера, затем задать пакет ошибок
  //   6. Переключить "Старт" канала в значение "1" и сразу в значение "0"
  //   8. Переключить "Старт" декодера в значение "1" и сразу в значение "0"
  //   contents of rom_1 (hex, n*v repeats v):
  //   94*1
  //   с не должно делиться на 2^m-1; 7 не делится на 15
  //   Кодовое слово
  //   g (x) = (x^7 + 1)*(x^4 + x + 1) = 1 + x + x^4 + x^7 + x^8 + x^11 
  //   Пакет ошибок
  //   contents of rom_2 (hex, n*v repeats v):
  //   4*1
  //   Кодовое слово*
  //   Выполнила
  //   ст.гр.961401
  //   Савченко Е.А.
endmodule

// Кодер
module \Кодер___Функциональная_схема  (
  input  \Вход ,
  input  \Старт ,
  output \Данные_для_записи_в_ОЗУ_кодера ,
  output \Данные_для_записи_в_буфер_канала ,
  output \Такты_для_ОЗУ_кодера ,
  output \Такты_для_буфера_канала ,
  output \Индикатор_окончания_работы_кодера ,
  output [6:0] \Шина_адреса_ПЗУ_кодера ,
  output [6:0] \Шина_адреса_ОЗУ_кодера ,
  output [6:0] \Шина_адреса_буфера_канала ,
  output \Очистка_ОЗУ_кодера ,
  output \Управление_буфером_канала 
);

  wire \генератор_кодера_1_переключение_ключей_после_k_94_тактов ;

  \Кодер__неполный  \u_кодер_неполный_1  (
    .\Вход (\Вход ), .\Такты (\Такты_для_буфера_канала ), .\Выход (\Данные_для_записи_в_буфер_канала ),
    .\Управление_ключами (\генератор_кодера_1_переключение_ключей_после_k_94_тактов ), .\Сброс (\Старт ));
  \Генератор_кодера  \u_генератор_кодера_1  (
    .\Старт (\Старт ),
    .\Переключение_ключей_после_k_94_тактов (\генератор_кодера_1_переключение_ключей_после_k_94_тактов ),
    .\Такты (\Такты_для_буфера_канала ),
    .\Индикатор_окончания_работы_кодера (\Индикатор_окончания_работы_кодера ),
    .\Шина_адреса_для_ОЗУ (\Шина_адреса_буфера_канала ), .\Шина_адреса_для_ПЗУ (\Шина_адреса_ПЗУ_кодера ));

  assign \Данные_для_записи_в_ОЗУ_кодера  = \Данные_для_записи_в_буфер_канала ;
  assign \Очистка_ОЗУ_кодера  = \Старт ;
  assign \Такты_для_ОЗУ_кодера  = \Такты_для_буфера_канала ;
  assign \Управление_буфером_канала  = \Старт ;
  assign \Шина_адреса_ОЗУ_кодера  = \Шина_адреса_буфера_канала ;

  // Notes on the sheet:
  //   Генератор (кодера)
  //   Кодер
endmodule

// Канал
module \Канал___Функциональная_схема  (
  input  \Управление_буфером_канала ,
  input  \Ошибки ,
  input  [6:0] \Шина_адреса_буфера_канала ,
  input  \Вход ,
  input  \Такты_кодера ,
  input  \Старт ,
  output \Кодовое_слово_с_ошибками ,
  output \Данные_для_записи_в_буфер_декодера ,
  output \Такты_для_ОЗУ_канала ,
  output \Такты_для_буфера_декодера ,
  output [6:0] \Шина_адреса_ПЗУ_канала ,
  output [6:0] \Шина_адреса_ОЗУ_канала ,
  output [6:0] \Шина_адреса_буфера_декодера ,
  output \Индикатор_окончания_работы_канала ,
  output \Очистка_ОЗУ_канала ,
  output \Управление_буфером_декодера 
);

  wire d_ff_1_q, or_1_out, ram_1_data;
  wire [6:0] \ключ_шины_адреса_1_выход ;

  \Генератор_канала  \u_генератор_канала_1  (
    .\Старт (\Старт ), .\Индикатор_окончания_работы_канала (\Индикатор_окончания_работы_канала ),
    .\Такты (\Такты_для_буфера_декодера ), .\Шина_адреса_ПЗУ_и_ОЗУ (\Шина_адреса_буфера_декодера ));
  \Ключ_шины_адреса  \u_ключ_шины_адреса_1  (
    .\Вход_1 (\Шина_адреса_буфера_канала ), .\Вход_2 (\Шина_адреса_буфера_декодера ),
    .\Выход (\ключ_шины_адреса_1_выход ), .\Управление_1 (\Управление_буфером_канала ),
    .\Управление_2 (\Старт ));
  D_Flip_Flop d_ff_1 (.Q(d_ff_1_q), .preset(\Управление_буфером_канала ), .reset(\Старт ));  // open: clk, D, Qn, en
  or or_1 (or_1_out, \Такты_кодера , \Такты_для_буфера_декодера );
  RAM #(.addrWidth(7), .dataWidth(1), .bus("separate")) ram_1 (
    .addr(\ключ_шины_адреса_1_выход ), .din(\Вход ), .data(ram_1_data), .str(d_ff_1_q), .clk(or_1_out));  // open: sel, ld, clr
  xor xor_1 (\Данные_для_записи_в_буфер_декодера , \Ошибки , ram_1_data);

  assign \Кодовое_слово_с_ошибками  = \Данные_для_записи_в_буфер_декодера ;
  assign \Очистка_ОЗУ_канала  = \Старт ;
  assign \Такты_для_ОЗУ_канала  = \Такты_для_буфера_декодера ;
  assign \Управление_буфером_декодера  = \Старт ;
  assign \Шина_адреса_ОЗУ_канала  = \Шина_адреса_буфера_декодера ;
  assign \Шина_адреса_ПЗУ_канала  = \Шина_адреса_буфера_декодера ;

  // Notes on the sheet:
  //   Генератор (канала)
  //   Буфер канала
  //   Режим работы буфера канала (запись или чтение)
endmodule

// Декодер
module \Декодер___Функциональная_схема  (
  input  [6:0] \Шина_адреса_буфера ,
  input  \Такты_канала ,
  input  \Управление_буфером ,
  input  \Вход ,
  input  \Старт ,
  output \Выход ,
  output [6:0] \Шина_адреса_ОЗУ ,
  output \Такты_для_ОЗУ ,
  output \Индикатор_окончания_работы_декодера ,
  output \Очистка_ОЗУ 
);

  wire not_1_out, or_1_out, ram_1_data, register_1_q, register_2_q, register_3_q, register_4_q, register_5_q,
       register_6_q, register_7_q, register_8_q, register_9_q, register_10_q, register_11_q, register_12_q,
       xor_1_out, xor_2_out, xor_3_out, xor_4_out, xor_6_out,
       \входной_буфер_декодера_1_кодовое_слово_с_ошибками ,
       \генератор_декодера_1_переключение_ключей_после_n_1_104_тактов , \генератор_декодера_1_такты ,
       \ключ_1_декодер_1_выход , \ключ_2_декодер_1_выход_1 , \ключ_2_декодер_1_выход_2 ;

  \Генератор_декодера  \u_генератор_декодера_1  (
    .\Старт (\Старт ), .\Индикатор_окончания_работы_декодера (\Индикатор_окончания_работы_декодера ),
    .\Переключение_ключей_после_n_1_104_тактов (\генератор_декодера_1_переключение_ключей_после_n_1_104_тактов ),
    .\Такты (\генератор_декодера_1_такты ), .\Шина_адреса_ОЗУ (\Шина_адреса_ОЗУ ));
  Register #(.width(1)) register_1 (
    .D(xor_6_out), .Q(register_1_q), .clk(\генератор_декодера_1_такты ), .clr(\Старт ));  // open: en
  xor xor_1 (xor_1_out, xor_6_out, register_1_q);
  Register #(.width(1)) register_2 (
    .D(xor_1_out), .Q(register_2_q), .clk(\генератор_декодера_1_такты ), .clr(\Старт ));  // open: en
  \Входной_буфер_декодера  \u_входной_буфер_декодера_1  (
    .\Управление_буфером_декодера (\Управление_буфером ),
    .\Шина_адреса_буфера_декодера (\Шина_адреса_буфера ), .\Вход (\Вход ), .\Такты_канала (\Такты_канала ),
    .\Такты_декодера (\генератор_декодера_1_такты ), .\Шина_адреса_ОЗУ (\Шина_адреса_ОЗУ ),
    .\Управление_ключом_шины_адреса (\Старт ),
    .\Кодовое_слово_с_ошибками (\входной_буфер_декодера_1_кодовое_слово_с_ошибками ));
  Register #(.width(1)) register_3 (
    .D(register_2_q), .Q(register_3_q), .clk(\генератор_декодера_1_такты ), .clr(\Старт ));  // open: en
  Register #(.width(1)) register_4 (
    .D(register_3_q), .Q(register_4_q), .clk(\генератор_декодера_1_такты ), .clr(\Старт ));  // open: en
  xor xor_2 (xor_2_out, xor_6_out, register_4_q);
  Register #(.width(1)) register_5 (
    .D(xor_2_out), .Q(register_5_q), .clk(\генератор_декодера_1_такты ), .clr(\Старт ));  // open: en
  Register #(.width(1)) register_6 (
    .D(register_5_q), .Q(register_6_q), .clk(\генератор_декодера_1_такты ), .clr(\Старт ));  // open: en
  not not_1 (not_1_out, \генератор_декодера_1_переключение_ключей_после_n_1_104_тактов );
  \Ключ_1__декодер  \u_ключ_1_декодер_1  (
    .\Управление (\генератор_декодера_1_переключение_ключей_после_n_1_104_тактов ),
    .\Вход (\входной_буфер_декодера_1_кодовое_слово_с_ошибками ), .\Выход (\ключ_1_декодер_1_выход ));
  Register #(.width(1)) register_7 (
    .D(register_6_q), .Q(register_7_q), .clk(\генератор_декодера_1_такты ), .clr(\Старт ));  // open: en
  RAM #(.addrWidth(7), .dataWidth(1), .bus("separate")) ram_1 (
    .addr(\Шина_адреса_ОЗУ ), .din(\входной_буфер_декодера_1_кодовое_слово_с_ошибками ), .data(ram_1_data),
    .str(not_1_out), .clk(\генератор_декодера_1_такты ));  // open: sel, ld, clr
  xor xor_3 (xor_3_out, xor_6_out, register_7_q);
  or or_1 (or_1_out, register_7_q, register_6_q, register_5_q, register_4_q, register_3_q, register_2_q, register_1_q);
  xor xor_4 (xor_4_out, xor_6_out, register_8_q);
  Register #(.width(1)) register_8 (
    .D(xor_3_out), .Q(register_8_q), .clk(\генератор_декодера_1_такты ), .clr(\Старт ));  // open: en
  xor xor_5 (\Выход , ram_1_data, register_12_q);
  Register #(.width(1)) register_9 (
    .D(xor_4_out), .Q(register_9_q), .clk(\генератор_декодера_1_такты ), .clr(\Старт ));  // open: en
  xor xor_6 (xor_6_out, \ключ_1_декодер_1_выход , \ключ_2_декодер_1_выход_1 );
  Register #(.width(1)) register_10 (
    .D(register_9_q), .Q(register_10_q), .clk(\генератор_декодера_1_такты ), .clr(\Старт ));  // open: en
  \Ключ_2__декодер  \u_ключ_2_декодер_1  (
    .\Управление (or_1_out), .\Выход_1 (\ключ_2_декодер_1_выход_1 ), .\Выход_2 (\ключ_2_декодер_1_выход_2 ),
    .\Вход (register_11_q),
    .\Блокировка_управления_на_первые_n_105_тактов (\генератор_декодера_1_переключение_ключей_после_n_1_104_тактов ));
  Register #(.width(1)) register_11 (
    .D(register_10_q), .Q(register_11_q), .clk(\генератор_декодера_1_такты ), .clr(\Старт ));  // open: en
  Register #(.width(1)) register_12 (
    .D(\ключ_2_декодер_1_выход_2 ), .Q(register_12_q), .clk(\генератор_декодера_1_такты ), .clr(\Старт ));  // open: en
  and and_1 (\Такты_для_ОЗУ , \генератор_декодера_1_такты , \генератор_декодера_1_переключение_ключей_после_n_1_104_тактов );

  assign \Очистка_ОЗУ  = \Старт ;

  // Notes on the sheet:
  //   Генератор (декодера)
  //   1+x+x^4+x^7+x^8+x^11
  //   Ключ 1
  //   Буфер
  //   Ключ 2
  //   Задержка на 1 такт
endmodule

module \Генератор_тактовый  (
  input  \Установка_в__0 ,
  output \Такты 
);

  wire clock_1_out, d_ff_1_q, d_ff_1_qn, d_ff_2_q, d_ff_2_qn;

  Clock clock_1 (.out(clock_1_out));
  D_Flip_Flop d_ff_1 (
    .clk(clock_1_out), .D(d_ff_1_qn), .Q(d_ff_1_q), .Qn(d_ff_1_qn), .reset(\Установка_в__0 ));  // open: preset, en
  D_Flip_Flop #(.trigger("falling")) d_ff_2 (
    .clk(clock_1_out), .D(d_ff_2_qn), .Q(d_ff_2_q), .Qn(d_ff_2_qn), .reset(\Установка_в__0 ));  // open: preset, en
  xor xor_1 (\Такты , d_ff_1_q, d_ff_2_q);

  // Notes on the sheet:
  //   Тактовый генератор Logisim при остановке может принять как "0", так и "1"
  //   При остановке в значении "1" нажатие на "Старт" добавляет ненужный такт
  //   Поэтому генератор должен сбрасываться в значение "0" при нажатии "Старт"
  //   Если использовать 1 триггер, то тактовая частота падает в 2 раза
  //   Первый триггер работает по переднему фронту, второй по заднему
endmodule

module \Генератор_кодера  (
  input  \Старт ,
  output [6:0] \Шина_адреса_для_ПЗУ ,
  output [6:0] \Шина_адреса_для_ОЗУ ,
  output \Переключение_ключей_после_k_94_тактов ,
  output \Индикатор_окончания_работы_кодера ,
  output \Такты 
);

  wire and_1_out, d_ff_1_q, d_ff_2_qn, \генератор_тактовый_1_такты , \Остановка_счета_out ,
       \Остановка_счета_после_переключения_ключей_out ;

  \Генератор_тактовый  \u_генератор_тактовый_1  (.\Такты (\генератор_тактовый_1_такты ), .\Установка_в__0 (\Старт ));
  Counter #(.width(7), .max('h69), .ongoal("stay")) counter_1 (
    .Q(\Шина_адреса_для_ПЗУ ), .clk(\Остановка_счета_после_переключения_ключей_out ), .clr(\Старт ));  // open: load, D, count, carry
  and \u_Остановка_счета_после_переключения_ключей  (\Остановка_счета_после_переключения_ключей_out , \Остановка_счета_out , ~\Переключение_ключей_после_k_94_тактов );  // AND_Gate
  Counter #(.width(7), .max('h69), .ongoal("stay")) counter_2 (
    .Q(\Шина_адреса_для_ОЗУ ), .clk(\Остановка_счета_out ), .clr(\Старт ));  // open: load, D, count, carry
  and \u_Остановка_счета  (\Остановка_счета_out , d_ff_1_q, \генератор_тактовый_1_такты , ~\Индикатор_окончания_работы_кодера );  // AND_Gate
  D_Flip_Flop d_ff_1 (.clk(\Старт ), .D(\Старт ), .Q(d_ff_1_q));  // open: Qn, preset, en, reset
  and and_1 (and_1_out, \Шина_адреса_для_ОЗУ [6], ~\Шина_адреса_для_ОЗУ [5], \Шина_адреса_для_ОЗУ [4], \Шина_адреса_для_ОЗУ [3], \Шина_адреса_для_ОЗУ [2], \Шина_адреса_для_ОЗУ [1], ~\Шина_адреса_для_ОЗУ [0]);  // AND_Gate
  and and_2 (\Индикатор_окончания_работы_кодера , \Шина_адреса_для_ОЗУ [6], \Шина_адреса_для_ОЗУ [5], ~\Шина_адреса_для_ОЗУ [4], \Шина_адреса_для_ОЗУ [3], ~\Шина_адреса_для_ОЗУ [2], ~\Шина_адреса_для_ОЗУ [1], \Шина_адреса_для_ОЗУ [0]);  // AND_Gate
  D_Flip_Flop #(.trigger("falling")) d_ff_2 (
    .clk(\генератор_тактовый_1_такты ), .D(and_1_out), .Q(\Переключение_ключей_после_k_94_тактов ),
    .Qn(d_ff_2_qn), .en(d_ff_2_qn), .reset(\Старт ));  // open: preset
  and and_3 (\Такты , d_ff_1_q, ~\Индикатор_окончания_работы_кодера , ~\Старт , \генератор_тактовый_1_такты );  // AND_Gate

  // Notes on the sheet:
  //   Счетчик тактов для ПЗУ
  //   Счетчик тактов для ОЗУ
  //   Блокировка
  //   произвольного
  //   запуска
  //   Генератор (тактовый)
  //   Остановка счета и подачи тактов при значении n=105
endmodule

module \Генератор_канала  (
  input  \Старт ,
  output [6:0] \Шина_адреса_ПЗУ_и_ОЗУ ,
  output \Индикатор_окончания_работы_канала ,
  output \Такты 
);

  wire d_ff_1_q, \генератор_тактовый_1_такты , \Остановка_счета_out ;

  \Генератор_тактовый  \u_генератор_тактовый_1  (.\Такты (\генератор_тактовый_1_такты ), .\Установка_в__0 (\Старт ));
  Counter #(.width(7), .max('h69), .ongoal("stay")) counter_1 (
    .Q(\Шина_адреса_ПЗУ_и_ОЗУ ), .clk(\Остановка_счета_out ), .clr(\Старт ));  // open: load, D, count, carry
  and \u_Остановка_счета  (\Остановка_счета_out , d_ff_1_q, \генератор_тактовый_1_такты , ~\Индикатор_окончания_работы_канала );  // AND_Gate
  D_Flip_Flop d_ff_1 (.clk(\Старт ), .D(\Старт ), .Q(d_ff_1_q));  // open: Qn, preset, en, reset
  and and_1 (\Индикатор_окончания_работы_канала , \Шина_адреса_ПЗУ_и_ОЗУ [6], \Шина_адреса_ПЗУ_и_ОЗУ [5], ~\Шина_адреса_ПЗУ_и_ОЗУ [4], \Шина_адреса_ПЗУ_и_ОЗУ [3], ~\Шина_адреса_ПЗУ_и_ОЗУ [2], ~\Шина_адреса_ПЗУ_и_ОЗУ [1], \Шина_адреса_ПЗУ_и_ОЗУ [0]);  // AND_Gate
  and and_2 (\Такты , d_ff_1_q, ~\Индикатор_окончания_работы_канала , ~\Старт , \генератор_тактовый_1_такты );  // AND_Gate

  // Notes on the sheet:
  //   Счетчик тактов
  //   Блокировка
  //   произвольного
  //   запуска
  //   Генератор (тактовый)
  //   Остановка счета и подачи тактов при n= 105
endmodule

module \Генератор_декодера  (
  input  \Старт ,
  output [6:0] \Шина_адреса_ОЗУ ,
  output \Переключение_ключей_после_n_1_104_тактов ,
  output \Индикатор_окончания_работы_декодера ,
  output \Такты 
);

  wire and_1_out, and_2_out, d_ff_1_q, d_ff_2_qn, \генератор_тактовый_1_такты , \Остановка_счета_out ;

  \Генератор_тактовый  \u_генератор_тактовый_1  (.\Такты (\генератор_тактовый_1_такты ), .\Установка_в__0 (\Старт ));
  Counter #(.width(7), .max('h69), .trigger("falling")) counter_1 (
    .Q(\Шина_адреса_ОЗУ ), .clk(\Остановка_счета_out ), .clr(\Старт ));  // open: load, D, count, carry
  and \u_Остановка_счета  (\Остановка_счета_out , d_ff_1_q, \генератор_тактовый_1_такты , ~\Индикатор_окончания_работы_декодера );  // AND_Gate
  D_Flip_Flop d_ff_1 (.clk(\Старт ), .D(\Старт ), .Q(d_ff_1_q));  // open: Qn, preset, en, reset
  and and_1 (and_1_out, \Шина_адреса_ОЗУ [6], \Шина_адреса_ОЗУ [5], ~\Шина_адреса_ОЗУ [4], \Шина_адреса_ОЗУ [3], ~\Шина_адреса_ОЗУ [2], ~\Шина_адреса_ОЗУ [1], ~\Шина_адреса_ОЗУ [0]);  // AND_Gate
  and and_2 (and_2_out, \Шина_адреса_ОЗУ [6], ~\Шина_адреса_ОЗУ [5], \Шина_адреса_ОЗУ [4], \Шина_адреса_ОЗУ [3], \Шина_адреса_ОЗУ [2], \Шина_адреса_ОЗУ [1], ~\Шина_адреса_ОЗУ [0]);  // AND_Gate
  D_Flip_Flop #(.trigger("falling")) d_ff_2 (
    .clk(\генератор_тактовый_1_такты ), .D(and_1_out), .Q(\Переключение_ключей_после_n_1_104_тактов ),
    .Qn(d_ff_2_qn), .en(d_ff_2_qn), .reset(\Старт ));  // open: preset
  and and_3 (\Индикатор_окончания_работы_декодера , and_2_out, \Переключение_ключей_после_n_1_104_тактов );
  and and_4 (\Такты , d_ff_1_q, ~\Индикатор_окончания_работы_декодера , ~\Старт , \генератор_тактовый_1_такты );  // AND_Gate

  // Notes on the sheet:
  //   Блокировка
  //   произвольного
  //   запуска
  //   Шина адреса
  //   cчет по заднему фронту
  //   закольцован после n=105 (69h)
  //   Генератор (тактовый)
  //   Остановка через k=94 тактов после переключения ключа 
endmodule

module \Кодер__неполный  (
  input  \Вход ,
  input  \Управление_ключами ,
  input  \Сброс ,
  input  \Такты ,
  output \Выход 
);

  wire register_1_q, register_2_q, register_3_q, register_4_q, register_5_q, register_6_q, register_7_q,
       register_8_q, register_9_q, register_10_q, register_11_q, xor_1_out, xor_2_out, xor_3_out, xor_4_out,
       xor_5_out, \ключ_1_кодер_1_выход ;

  Register #(.width(1)) register_1 (
    .D(\ключ_1_кодер_1_выход ), .Q(register_1_q), .clk(\Такты ), .clr(\Сброс ));  // open: en
  xor xor_1 (xor_1_out, \ключ_1_кодер_1_выход , register_1_q);
  Register #(.width(1)) register_2 (.D(xor_1_out), .Q(register_2_q), .clk(\Такты ), .clr(\Сброс ));  // open: en
  Register #(.width(1)) register_3 (.D(register_2_q), .Q(register_3_q), .clk(\Такты ), .clr(\Сброс ));  // open: en
  Register #(.width(1)) register_4 (.D(register_3_q), .Q(register_4_q), .clk(\Такты ), .clr(\Сброс ));  // open: en
  xor xor_2 (xor_2_out, \ключ_1_кодер_1_выход , register_4_q);
  Register #(.width(1)) register_5 (.D(xor_2_out), .Q(register_5_q), .clk(\Такты ), .clr(\Сброс ));  // open: en
  Register #(.width(1)) register_6 (.D(register_5_q), .Q(register_6_q), .clk(\Такты ), .clr(\Сброс ));  // open: en
  Register #(.width(1)) register_7 (.D(register_6_q), .Q(register_7_q), .clk(\Такты ), .clr(\Сброс ));  // open: en
  xor xor_3 (xor_3_out, \ключ_1_кодер_1_выход , register_7_q);
  xor xor_4 (xor_4_out, \ключ_1_кодер_1_выход , register_8_q);
  Register #(.width(1)) register_8 (.D(xor_3_out), .Q(register_8_q), .clk(\Такты ), .clr(\Сброс ));  // open: en
  Register #(.width(1)) register_9 (.D(xor_4_out), .Q(register_9_q), .clk(\Такты ), .clr(\Сброс ));  // open: en
  Register #(.width(1)) register_10 (.D(register_9_q), .Q(register_10_q), .clk(\Такты ), .clr(\Сброс ));  // open: en
  \Ключ_1__кодер  \u_ключ_1_кодер_1  (
    .\Выход (\ключ_1_кодер_1_выход ), .\Управление (\Управление_ключами ), .\Вход (xor_5_out));
  Register #(.width(1)) register_11 (.D(register_10_q), .Q(register_11_q), .clk(\Такты ), .clr(\Сброс ));  // open: en
  xor xor_5 (xor_5_out, \Вход , register_11_q);
  \Ключ_2__кодер  \u_ключ_2_кодер_1  (
    .\Вход_1 (\Вход ), .\Управление (\Управление_ключами ), .\Вход_2 (register_11_q), .\Выход (\Выход ));

  // Notes on the sheet:
  //   1+x+x^4+x^7+x^8+x^11
  //   Кодер разделимого циклического кода
  //   с последовательной обработкой данных
  //   Ключ 1
  //   Ключ 2
endmodule

module \Ключ_1__кодер  (
  input  \Управление ,
  input  \Вход ,
  output \Выход 
);

  and and_1 (\Выход , ~\Управление , \Вход );  // AND_Gate
endmodule

module \Ключ_2__кодер  (
  input  \Вход_1 ,
  input  \Управление ,
  input  \Вход_2 ,
  output \Выход 
);

  wire and_1_out, and_2_out;

  and and_1 (and_1_out, \Вход_1 , ~\Управление );  // AND_Gate
  or or_1 (\Выход , and_1_out, and_2_out);
  and and_2 (and_2_out, \Управление , \Вход_2 );
endmodule

module \Ключ_1__декодер  (
  input  \Управление ,
  input  \Вход ,
  output \Выход 
);

  and and_1 (\Выход , ~\Управление , \Вход );  // AND_Gate
endmodule

module \Ключ_2__декодер  (
  input  \Вход ,
  input  \Управление ,
  input  \Блокировка_управления_на_первые_n_105_тактов ,
  output \Выход_1 ,
  output \Выход_2 
);

  wire or_1_out;

  and and_1 (\Выход_1 , \Вход , or_1_out);
  or or_1 (or_1_out, \Управление , ~\Блокировка_управления_на_первые_n_105_тактов );  // OR_Gate
  and and_2 (\Выход_2 , ~or_1_out, \Вход );  // AND_Gate
endmodule

module \Ключ_шины_адреса  (
  input  [6:0] \Вход_1 ,
  input  [6:0] \Вход_2 ,
  input  \Управление_1 ,
  input  \Управление_2 ,
  output [6:0] \Выход 
);

  wire and_1_out, and_2_out, and_3_out, and_4_out, and_5_out, and_6_out, and_7_out, and_8_out, and_9_out,
       and_10_out, and_11_out, and_12_out, and_13_out, and_14_out, d_ff_1_q;

  D_Flip_Flop d_ff_1 (.Q(d_ff_1_q), .preset(\Управление_1 ), .reset(\Управление_2 ));  // open: clk, D, Qn, en
  and and_1 (and_1_out, \Вход_1 [0], d_ff_1_q);
  and and_2 (and_2_out, ~d_ff_1_q, \Вход_2 [0]);  // AND_Gate
  and and_3 (and_3_out, \Вход_1 [1], d_ff_1_q);
  and and_4 (and_4_out, ~d_ff_1_q, \Вход_2 [1]);  // AND_Gate
  and and_5 (and_5_out, \Вход_1 [2], d_ff_1_q);
  and and_6 (and_6_out, ~d_ff_1_q, \Вход_2 [2]);  // AND_Gate
  and and_7 (and_7_out, \Вход_1 [3], d_ff_1_q);
  and and_8 (and_8_out, ~d_ff_1_q, \Вход_2 [3]);  // AND_Gate
  and and_9 (and_9_out, \Вход_1 [4], d_ff_1_q);
  and and_10 (and_10_out, ~d_ff_1_q, \Вход_2 [4]);  // AND_Gate
  and and_11 (and_11_out, \Вход_1 [5], d_ff_1_q);
  and and_12 (and_12_out, ~d_ff_1_q, \Вход_2 [5]);  // AND_Gate
  and and_13 (and_13_out, \Вход_1 [6], d_ff_1_q);
  and and_14 (and_14_out, ~d_ff_1_q, \Вход_2 [6]);  // AND_Gate
  or or_1 (\Выход [6], and_1_out, and_2_out);
  or or_2 (\Выход [5], and_3_out, and_4_out);
  or or_3 (\Выход [4], and_5_out, and_6_out);
  or or_4 (\Выход [3], and_7_out, and_8_out);
  or or_5 (\Выход [2], and_9_out, and_10_out);
  or or_6 (\Выход [1], and_11_out, and_12_out);
  or or_7 (\Выход [0], and_13_out, and_14_out);
endmodule

module \Входной_буфер_декодера  (
  input  \Управление_буфером_декодера ,
  input  [6:0] \Шина_адреса_буфера_декодера ,
  input  \Вход ,
  input  \Такты_канала ,
  input  \Такты_декодера ,
  input  [6:0] \Шина_адреса_ОЗУ ,
  input  \Управление_ключом_шины_адреса ,
  output \Кодовое_слово_с_ошибками 
);

  wire d_ff_1_q, or_1_out;
  wire [6:0] \ключ_шины_адреса_1_выход ;

  \Ключ_шины_адреса  \u_ключ_шины_адреса_1  (
    .\Вход_1 (\Шина_адреса_буфера_декодера ), .\Вход_2 (\Шина_адреса_ОЗУ ),
    .\Выход (\ключ_шины_адреса_1_выход ), .\Управление_1 (\Управление_буфером_декодера ),
    .\Управление_2 (\Управление_ключом_шины_адреса ));
  D_Flip_Flop d_ff_1 (
    .Q(d_ff_1_q), .preset(\Управление_буфером_декодера ), .reset(\Управление_ключом_шины_адреса ));  // open: clk, D, Qn, en
  or or_1 (or_1_out, \Такты_канала , \Такты_декодера );
  RAM #(.addrWidth(7), .dataWidth(1), .bus("separate")) ram_1 (
    .addr(\ключ_шины_адреса_1_выход ), .din(\Вход ), .data(\Кодовое_слово_с_ошибками ), .str(d_ff_1_q),
    .clk(or_1_out));  // open: sel, ld, clr

  // Notes on the sheet:
  //   Ключ шины адреса
  //   Буфер декодера
  //   Режим работы буфера декодера (запись или чтение)
endmodule
