// Logisim project pract2-2.circ as structural Verilog: 5 circuits, main circuit Структурная схема кодека
module \Структурная_схема_кодека  (
  input  i1,
  input  e1,
  input  e2,
  input  i2,
  input  e3,
  input  i3,
  input  e4,
  input  e5,
  input  i4,
  input  e6,
  input  e7,
  input  e8,
  output \с1 ,
  output \с1_star ,
  output \с2 ,
  output \с2_star ,
  output i1_star,
  output \с3 ,
  output \с3_star ,
  output i2_star,
  output \с4 ,
  output \с4_star ,
  output i3_star,
  output \с5 ,
  output \с5_star ,
  output i4_star,
  output \с6 ,
  output \с6_star ,
  output \с7 ,
  output \с7_star ,
  output \с8 ,
  output \с8_star 
);

  wire \функциональная_схема_мажоритарного_декодера_1_out_4 ;
  wire [7:0] \функциональная_схема_канала_1_out_18 , \функциональная_схема_кодера_1_out_13 ;

  \Функциональная_схема_кодера  \u_функциональная_схема_кодера_1  (
    .i1(i1), .i2(i2), .i3(i3), .i4(i4), .c1(\с1 ), .c2(\с2 ), .c3(\с3 ), .c4(\с4 ), .c5(\с5 ), .c6(\с6 ),
    .c7(\с7 ), .c8(\с8 ), .out_13(\функциональная_схема_кодера_1_out_13 ));
  \Функциональная_схема_канала  \u_функциональная_схема_канала_1  (
    .e1(e1), .e2(e2), .e3(e3), .e4(e4), .e5(e5), .e6(e6), .e7(e7), .e8(e8),
    .in_9(\функциональная_схема_кодера_1_out_13 ), .c1_star(\с1_star ), .c2_star(\с2_star ),
    .c3_star(\с3_star ), .c4_star(\с4_star ), .c5_star(\с5_star ), .c6_star(\с6_star ), .c7_star(\с7_star ),
    .c8_star(\с8_star ), .out_18(\функциональная_схема_канала_1_out_18 ));
  \Функциональная_схема_мажоритарного_декодера  \u_функциональная_схема_мажоритарного_декодера_1  (
    .in_1(\функциональная_схема_канала_1_out_18 ), .i1_star(i1_star), .i2_star(i2_star), .i3_star(i3_star),
    .i4_star(i4_star), .out_4(\функциональная_схема_мажоритарного_декодера_1_out_4 ));
  LED led_1 (.in(\функциональная_схема_мажоритарного_декодера_1_out_4 ));

  // Notes on the sheet:
  //   Мажоритарный кодек кода
  //   *
  //   s1
  //   n=8 длина кода
  //   Выполнили
  //   Савич О.А.
  //   исходные данные
  //   m=3 натуральное число
  //   l=1 порядок кода
  //   d=4 кодовое расстояние
  //   ст.гр.961401
  //   Савченко Е.А.
  //   Перминова А.В
  //   Матошко М.П.
  //   k=4 количество информационых разрядов
  //   r=4 количество проверочных разрядов
  //   tобн<= 3 кратность обнаружения ошибок
  //   tисп= 1 кратность исправления ошибок
endmodule

module \Функциональная_схема_кодера  (
  input  i1,
  input  i2,
  input  i3,
  input  i4,
  output c1,
  output c2,
  output c3,
  output c4,
  output c5,
  output c6,
  output c7,
  output c8,
  output [7:0] out_13
);

  xor xor_1 (c2, i1, i4);
  xor xor_2 (c3, i1, i3);
  xor xor_3 (c4, i1, i3, i4);
  xor xor_4 (c5, i1, i2);
  xor xor_5 (c6, i1, i2, i4);
  xor xor_6 (c7, i1, i2, i3);
  xor xor_7 (c8, i1, i2, i3, i4);

  assign c1 = i1;
  assign out_13 = {i1, c2, c3, c4, c5, c6, c7, c8};
endmodule

module \Функциональная_схема_канала  (
  input  e1,
  input  e2,
  input  e3,
  input  e4,
  input  e5,
  input  e6,
  input  e7,
  input  e8,
  input  [7:0] in_9,
  output c1_star,
  output c2_star,
  output c3_star,
  output c4_star,
  output c5_star,
  output c6_star,
  output c7_star,
  output c8_star,
  output [7:0] out_18
);

  xor xor_1 (c1_star, e1, in_9[7]);
  xor xor_2 (c2_star, e2, in_9[6]);
  xor xor_3 (c3_star, e3, in_9[5]);
  xor xor_4 (c4_star, e4, in_9[4]);
  xor xor_5 (c5_star, e5, in_9[3]);
  xor xor_6 (c6_star, e6, in_9[2]);
  xor xor_7 (c7_star, e7, in_9[1]);
  xor xor_8 (c8_star, e8, in_9[0]);

  assign out_18 = {c1_star, c2_star, c3_star, c4_star, c5_star, c6_star, c7_star, c8_star};
endmodule

module \Функциональная_схема_мажоритарного_декодера  (
  input  [7:0] in_1,
  output i1_star,
  output i2_star,
  output out_4,
  output i3_star,
  output i4_star
);

  wire xor_1_out, xor_2_out, xor_3_out, xor_4_out, xor_5_out, xor_6_out, xor_7_out, xor_8_out, xor_9_out,
       xor_10_out, xor_11_out, xor_12_out, xor_13_out, xor_14_out, xor_15_out,
       \мажоритарный_элемент_на_четыри_входа_1_out_6 , \мажоритарный_элемент_на_четыри_входа_2_out_6 ,
       \мажоритарный_элемент_на_четыри_входа_3_out_6 , \мажоритарный_элемент_на_четыри_входа_4_out_6 ;

  xor xor_1 (xor_1_out, in_1[3], in_1[7]);
  xor xor_2 (xor_2_out, in_1[2], in_1[6]);
  xor xor_3 (xor_3_out, in_1[1], in_1[5]);
  xor xor_4 (xor_4_out, in_1[0], in_1[4]);
  xor xor_5 (xor_5_out, in_1[5], in_1[7]);
  xor xor_6 (xor_6_out, in_1[4], in_1[6]);
  xor xor_7 (xor_7_out, in_1[1], in_1[3]);
  xor xor_8 (xor_8_out, in_1[0], in_1[2]);
  xor xor_9 (xor_9_out, in_1[6], in_1[7]);
  xor xor_10 (xor_10_out, in_1[4], in_1[5]);
  xor xor_11 (xor_11_out, in_1[2], in_1[3]);
  xor xor_12 (xor_12_out, in_1[0], in_1[1]);
  \Мажоритарный_элемент_на_четыри_входа  \u_мажоритарный_элемент_на_четыри_входа_1  (
    .in_1(xor_1_out), .in_2(xor_2_out), .in_3(xor_3_out), .in_4(xor_4_out), .out_5(i2_star),
    .out_6(\мажоритарный_элемент_на_четыри_входа_1_out_6 ));
  \Мажоритарный_элемент_на_четыри_входа  \u_мажоритарный_элемент_на_четыри_входа_2  (
    .in_1(xor_5_out), .in_2(xor_6_out), .in_3(xor_7_out), .in_4(xor_8_out), .out_5(i3_star),
    .out_6(\мажоритарный_элемент_на_четыри_входа_2_out_6 ));
  \Мажоритарный_элемент_на_четыри_входа  \u_мажоритарный_элемент_на_четыри_входа_3  (
    .in_1(xor_9_out), .in_2(xor_10_out), .in_3(xor_11_out), .in_4(xor_12_out), .out_5(i4_star),
    .out_6(\мажоритарный_элемент_на_четыри_входа_3_out_6 ));
  xor xor_13 (xor_13_out, in_1[3], i2_star);
  xor xor_14 (xor_14_out, i3_star, in_1[5]);
  xor xor_15 (xor_15_out, i4_star, in_1[6]);
  \Мажоритарный_элемент_на_четыри_входа  \u_мажоритарный_элемент_на_четыри_входа_4  (
    .in_1(in_1[7]), .in_2(xor_13_out), .in_3(xor_14_out), .in_4(xor_15_out), .out_5(i1_star),
    .out_6(\мажоритарный_элемент_на_четыри_входа_4_out_6 ));
  or or_1 (out_4, \мажоритарный_элемент_на_четыри_входа_4_out_6 , \мажоритарный_элемент_на_четыри_входа_1_out_6 , \мажоритарный_элемент_на_четыри_входа_2_out_6 , \мажоритарный_элемент_на_четыри_входа_3_out_6 );
endmodule

module \Мажоритарный_элемент_на_четыри_входа  (
  input  in_1,
  input  in_2,
  input  in_3,
  input  in_4,
  output out_5,
  output out_6
);

  wire [2:0] bitadder_1_out;

  BitAdder #(.width(1)) bitadder_1 (.in0(in_1), .in1(in_2), .in2(in_3), .in3(in_4), .out(bitadder_1_out));
  Comparator #(.width(3), .mode("unsigned")) comparator_1 (
    .a(bitadder_1_out), .b(3'b010), .gt(out_5), .eq(out_6));  // open: lt
endmodule
