// Logisim project LR3_3.circ as structural Verilog: 4 circuits, main circuit Структурная схема кодека
module \Структурная_схема_кодека  (
  input  i1,
  input  e1,
  input  i2,
  input  e2,
  input  i3,
  input  e3,
  input  i4,
  input  e4,
  input  i5,
  input  e5,
  input  i6,
  input  e6,
  input  i7,
  input  e7,
  input  i8,
  input  e8,
  input  i9,
  input  e9,
  input  i10,
  input  e10,
  input  i11,
  input  e11,
  input  i12,
  input  e12,
  input  i13,
  input  e13,
  input  i14,
  input  e14,
  input  i15,
  input  e15,
  input  i16,
  input  e16,
  input  i17,
  input  e17,
  input  i18,
  input  e18,
  input  i19,
  input  e19,
  input  i20,
  input  e20,
  input  i21,
  input  e21,
  input  e22,
  input  e23,
  input  e24,
  input  e25,
  input  e26,
  input  e27,
  output \с1 ,
  output \с1_star ,
  output i1_star,
  output \с2 ,
  output \с2_star ,
  output i2_star,
  output \с3 ,
  output \с3_star ,
  output i3_star,
  output \с4 ,
  output \с4_star ,
  output i4_star,
  output \с5 ,
  output \с5_star ,
  output i5_star,
  output \с6 ,
  output \с6_star ,
  output i6_star,
  output \с7 ,
  output \с7_star ,
  output i7_star,
  output \с8 ,
  output \с8_star ,
  output i8_star,
  output \с9 ,
  output \с9_star ,
  output i9_star,
  output \с10 ,
  output \с10_star ,
  output i10_star,
  output \с11 ,
  output \с11_star ,
  output i11_star,
  output \с12 ,
  output \с12_star ,
  output i12_star,
  output \с13 ,
  output \с13_star ,
  output i13_star,
  output \с14 ,
  output \с14_star ,
  output i14_star,
  output \с15 ,
  output \с15_star ,
  output i15_star,
  output \с16 ,
  output \с16_star ,
  output i16_star,
  output \с17 ,
  output \с17_star ,
  output i17_star,
  output \с18 ,
  output \с18_star ,
  output i18_star,
  output \с19 ,
  output \с19_star ,
  output i19_star,
  output \с20 ,
  output \с20_star ,
  output i20_star,
  output \с21 ,
  output \с21_star ,
  output i21_star,
  output \с22 ,
  output \с22_star ,
  output \с23 ,
  output \с23_star ,
  output \с24 ,
  output \с24_star ,
  output \с25 ,
  output \с25_star ,
  output \с26 ,
  output \с26_star ,
  output \с27 ,
  output \с27_star 
);

  wire \функциональная_схема_синдромного_декодера_1_s1 , \функциональная_схема_синдромного_декодера_1_s2 ,
       \функциональная_схема_синдромного_декодера_1_s3 , \функциональная_схема_синдромного_декодера_1_s4 ,
       \функциональная_схема_синдромного_декодера_1_s5 , \функциональная_схема_синдромного_декодера_1_s6 ;
  wire [26:0] \функциональная_схема_канала_1_out_56 , \функциональная_схема_кодера_1_out_49 ;

  \Функциональная_схема_кодера  \u_функциональная_схема_кодера_1  (
    .i1(i1), .i2(i2), .i3(i3), .i4(i4), .i5(i5), .i6(i6), .i7(i7), .i8(i8), .i9(i9), .i10(i10), .i11(i11),
    .i12(i12), .i13(i13), .i14(i14), .i15(i15), .i16(i16), .i17(i17), .i18(i18), .i19(i19), .i20(i20),
    .i21(i21), .\с1 (\с1 ), .\с2 (\с2 ), .\с3 (\с3 ), .\с4 (\с4 ), .\с5 (\с5 ), .\с6 (\с6 ), .\с7 (\с7 ),
    .\с8 (\с8 ), .\с9 (\с9 ), .\с10 (\с10 ), .\с11 (\с11 ), .\с12 (\с12 ), .\с13 (\с13 ), .\с14 (\с14 ),
    .\с15 (\с15 ), .\с16 (\с16 ), .\с17 (\с17 ), .\с18 (\с18 ), .\с19 (\с19 ), .\с20 (\с20 ), .\с21 (\с21 ),
    .\с22 (\с22 ), .\с23 (\с23 ), .\с24 (\с24 ), .\с25 (\с25 ), .\с26 (\с26 ), .\с27 (\с27 ),
    .out_49(\функциональная_схема_кодера_1_out_49 ));
  \Функциональная_схема_канала  \u_функциональная_схема_канала_1  (
    .e1(e1), .e2(e2), .e3(e3), .e4(e4), .e5(e5), .e6(e6), .e7(e7), .e8(e8), .e9(e9), .e10(e10), .e11(e11),
    .e12(e12), .e13(e13), .e14(e14), .e15(e15), .e16(e16), .e17(e17), .e18(e18), .e19(e19), .e20(e20),
    .e21(e21), .e22(e22), .e23(e23), .e24(e24), .e25(e25), .e26(e26), .e27(e27),
    .in_28(\функциональная_схема_кодера_1_out_49 ), .c1_star(\с1_star ), .c2_star(\с2_star ),
    .c3_star(\с3_star ), .c4_star(\с4_star ), .c5_star(\с5_star ), .c6_star(\с6_star ), .c7_star(\с7_star ),
    .c8_star(\с8_star ), .c9_star(\с9_star ), .c10_star(\с10_star ), .c11_star(\с11_star ),
    .c12_star(\с12_star ), .c13_star(\с13_star ), .c14_star(\с14_star ), .c15_star(\с15_star ),
    .c16_star(\с16_star ), .c17_star(\с17_star ), .c18_star(\с18_star ), .c19_star(\с19_star ),
    .c20_star(\с20_star ), .c21_star(\с21_star ), .c22_star(\с22_star ), .c23_star(\с23_star ),
    .c24_star(\с24_star ), .c25_star(\с25_star ), .c26_star(\с26_star ), .c27_star(\с27_star ),
    .out_56(\функциональная_схема_канала_1_out_56 ));
  \Функциональная_схема_синдромного_декодера  \u_функциональная_схема_синдромного_декодера_1  (
    .in_1(\функциональная_схема_канала_1_out_56 ), .i1_star(i1_star), .i2_star(i2_star), .i3_star(i3_star),
    .i4_star(i4_star), .i5_star(i5_star), .i6_star(i6_star), .i7_star(i7_star), .i8_star(i8_star),
    .i9_star(i9_star), .i10_star(i10_star), .i11_star(i11_star), .i12_star(i12_star), .i13_star(i13_star),
    .i14_star(i14_star), .i15_star(i15_star), .i16_star(i16_star), .i17_star(i17_star), .i18_star(i18_star),
    .i19_star(i19_star), .i20_star(i20_star), .i21_star(i21_star),
    .s1(\функциональная_схема_синдромного_декодера_1_s1 ),
    .s2(\функциональная_схема_синдромного_декодера_1_s2 ),
    .s3(\функциональная_схема_синдромного_декодера_1_s3 ),
    .s4(\функциональная_схема_синдромного_декодера_1_s4 ),
    .s5(\функциональная_схема_синдромного_декодера_1_s5 ),
    .s6(\функциональная_схема_синдромного_декодера_1_s6 ));
  LED led_1 (.in(\функциональная_схема_синдромного_декодера_1_s6 ));
  LED led_2 (.in(\функциональная_схема_синдромного_декодера_1_s5 ));
  LED led_3 (.in(\функциональная_схема_синдромного_декодера_1_s4 ));
  LED led_4 (.in(\функциональная_схема_синдромного_декодера_1_s3 ));
  LED led_5 (.in(\функциональная_схема_синдромного_декодера_1_s2 ));
  LED led_6 (.in(\функциональная_схема_синдромного_декодера_1_s1 ));

  // Notes on the sheet:
  //   Кодер
  //   Синдромный кодек Рида-Соломона
  //   Канал
  //   *
  //   *
  //   Декодер
  //   s1
  //   s3
  //   s4
  //   s5
  //   s2
  //   s6
  //   b=3 длина модуля
  //   n=27 длина кода
  //   p(x)=1+x+x
  //   Перминова Анна
  //   Матошко Мария
  //   Савченко Екатерина
  //   Савич Ольга
  //   r=6 количество проверочных разрядов
  //   d=3 модульное кодовое расстояние
  //   t=1 кратность исправляемых ошибок
  //   3
  //   Выполнили ст. гр. 961401:
  //   k=21 количество информационых разрядов
endmodule

module \Функциональная_схема_кодера  (
  input  i1,
  input  i2,
  input  i3,
  input  i4,
  input  i5,
  input  i6,
  input  i7,
  input  i8,
  input  i9,
  input  i10,
  input  i11,
  input  i12,
  input  i13,
  input  i14,
  input  i15,
  input  i16,
  input  i17,
  input  i18,
  input  i19,
  input  i20,
  input  i21,
  output \с1 ,
  output \с2 ,
  output \с3 ,
  output \с4 ,
  output \с5 ,
  output \с6 ,
  output \с7 ,
  output \с8 ,
  output \с9 ,
  output \с10 ,
  output \с11 ,
  output \с12 ,
  output \с13 ,
  output \с14 ,
  output \с15 ,
  output \с16 ,
  output \с17 ,
  output \с18 ,
  output \с19 ,
  output \с20 ,
  output \с21 ,
  output \с22 ,
  output \с23 ,
  output \с24 ,
  output \с25 ,
  output \с26 ,
  output \с27 ,
  output [26:0] out_49
);

  ExactlyOne xor_1 (.out(out_49[5]), .in0(i1), .in1(i4), .in2(i7), .in3(i10), .in4(i13), .in5(i16), .in6(i19));
  ExactlyOne xor_2 (.out(out_49[4]), .in0(i2), .in1(i5), .in2(i8), .in3(i11), .in4(i14), .in5(i17), .in6(i20));
  ExactlyOne xor_3 (.out(out_49[3]), .in0(i3), .in1(i6), .in2(i9), .in3(i12), .in4(i15), .in5(i18), .in6(i21));
  ExactlyOne xor_4 (
    .out(out_49[2]), .in0(i1), .in1(i5), .in2(i7), .in3(i9), .in4(i10), .in5(i11), .in6(i13), .in7(i14),
    .in8(i15), .in9(i17), .in10(i18), .in11(i21));
  ExactlyOne xor_5 (
    .out(out_49[1]), .in0(i2), .in1(i4), .in2(i6), .in3(i7), .in4(i8), .in5(i10), .in6(i11), .in7(i12),
    .in8(i14), .in9(i15), .in10(i18), .in11(i19));
  ExactlyOne xor_6 (
    .out(out_49[0]), .in0(i3), .in1(i4), .in2(i8), .in3(i10), .in4(i12), .in5(i13), .in6(i14), .in7(i16),
    .in8(i17), .in9(i18), .in10(i20), .in11(i21));

  assign out_49[26:6] = {i1, i2, i3, i4, i5, i6, i7, i8, i9, i10, i11, i12, i13, i14, i15, i16, i17, i18, i19, i20, i21};
  assign \с1  = i1;
  assign \с2  = i2;
  assign \с3  = i3;
  assign \с4  = i4;
  assign \с5  = i5;
  assign \с6  = i6;
  assign \с7  = i7;
  assign \с8  = i8;
  assign \с9  = i9;
  assign \с10  = i10;
  assign \с11  = i11;
  assign \с12  = i12;
  assign \с13  = i13;
  assign \с14  = i14;
  assign \с15  = i15;
  assign \с16  = i16;
  assign \с17  = i17;
  assign \с18  = i18;
  assign \с19  = i19;
  assign \с20  = i20;
  assign \с21  = i21;
  assign \с22  = out_49[5];
  assign \с23  = out_49[4];
  assign \с24  = out_49[3];
  assign \с25  = out_49[2];
  assign \с26  = out_49[1];
  assign \с27  = out_49[0];
endmodule

module \Функциональная_схема_канала  (
  input  e1,
  input  e2,
  input  e3,
  input  e4,
  input  e5,
  input  e6,
  input  e7,
  input  e8,
  input  e9,
  input  e10,
  input  e11,
  input  e12,
  input  e13,
  input  e14,
  input  e15,
  input  e16,
  input  e17,
  input  e18,
  input  e19,
  input  e20,
  input  e21,
  input  e22,
  input  e23,
  input  e24,
  input  e25,
  input  e26,
  input  e27,
  input  [26:0] in_28,
  output c1_star,
  output c2_star,
  output c3_star,
  output c4_star,
  output c5_star,
  output c6_star,
  output c7_star,
  output c8_star,
  output c9_star,
  output c10_star,
  output c11_star,
  output c12_star,
  output c13_star,
  output c14_star,
  output c15_star,
  output c16_star,
  output c17_star,
  output c18_star,
  output c19_star,
  output c20_star,
  output c21_star,
  output c22_star,
  output c23_star,
  output c24_star,
  output c25_star,
  output c26_star,
  output c27_star,
  output [26:0] out_56
);

  xor xor_1 (c27_star, e27, in_28[0]);
  xor xor_2 (c19_star, e19, in_28[8]);
  xor xor_3 (c20_star, e20, in_28[7]);
  xor xor_4 (c21_star, e21, in_28[6]);
  xor xor_5 (c22_star, e22, in_28[5]);
  xor xor_6 (c23_star, e23, in_28[4]);
  xor xor_7 (c24_star, e24, in_28[3]);
  xor xor_8 (c25_star, e25, in_28[2]);
  xor xor_9 (c26_star, e26, in_28[1]);
  xor xor_10 (c11_star, e11, in_28[16]);
  xor xor_11 (c12_star, e12, in_28[15]);
  xor xor_12 (c13_star, e13, in_28[14]);
  xor xor_13 (c14_star, e14, in_28[13]);
  xor xor_14 (c15_star, e15, in_28[12]);
  xor xor_15 (c16_star, e16, in_28[11]);
  xor xor_16 (c17_star, e17, in_28[10]);
  xor xor_17 (c18_star, e18, in_28[9]);
  xor xor_18 (c3_star, e3, in_28[24]);
  xor xor_19 (c4_star, e4, in_28[23]);
  xor xor_20 (c5_star, e5, in_28[22]);
  xor xor_21 (c6_star, e6, in_28[21]);
  xor xor_22 (c7_star, e7, in_28[20]);
  xor xor_23 (c8_star, e8, in_28[19]);
  xor xor_24 (c9_star, e9, in_28[18]);
  xor xor_25 (c10_star, e10, in_28[17]);
  xor xor_26 (c1_star, e1, in_28[26]);
  xor xor_27 (c2_star, e2, in_28[25]);

  assign out_56 = {c1_star, c2_star, c3_star, c4_star, c5_star, c6_star, c7_star, c8_star, c9_star, c10_star, c11_star, c12_star, c13_star, c14_star, c15_star, c16_star, c17_star, c18_star, c19_star, c20_star, c21_star, c22_star, c23_star, c24_star, c25_star, c26_star, c27_star};
endmodule

module \Функциональная_схема_синдромного_декодера  (
  input  [26:0] in_1,
  output i1_star,
  output i2_star,
  output i3_star,
  output i4_star,
  output i5_star,
  output i6_star,
  output i7_star,
  output i8_star,
  output i9_star,
  output i10_star,
  output i11_star,
  output i12_star,
  output i13_star,
  output i14_star,
  output i15_star,
  output i16_star,
  output i17_star,
  output i18_star,
  output i19_star,
  output i20_star,
  output i21_star,
  output s1,
  output s2,
  output s3,
  output s4,
  output s5,
  output s6
);

  wire [26:0] rom_1_data;

  xor xor_1 (s1, in_1[26], in_1[23], in_1[20], in_1[17], in_1[14], in_1[11], in_1[8], in_1[5]);
  xor xor_2 (s2, in_1[25], in_1[22], in_1[19], in_1[16], in_1[13], in_1[10], in_1[7], in_1[4]);
  xor xor_3 (s3, in_1[24], in_1[21], in_1[18], in_1[15], in_1[12], in_1[9], in_1[6], in_1[3]);
  xor xor_4 (s4, in_1[26], in_1[22], in_1[20], in_1[18], in_1[17], in_1[16], in_1[14], in_1[13], in_1[12], in_1[10], in_1[9], in_1[6], in_1[2]);
  xor xor_5 (s5, in_1[25], in_1[23], in_1[21], in_1[20], in_1[19], in_1[17], in_1[16], in_1[15], in_1[13], in_1[12], in_1[9], in_1[8], in_1[1]);
  xor xor_6 (s6, in_1[24], in_1[23], in_1[19], in_1[17], in_1[15], in_1[14], in_1[13], in_1[11], in_1[10], in_1[9], in_1[7], in_1[6], in_1[0]);
  ROM #(.addrWidth(6), .dataWidth(27)) rom_1 (.addr({s1, s2, s3, s4, s5, s6}), .data(rom_1_data), .sel(1'b1));
  xor xor_7 (i20_star, in_1[7], rom_1_data[7]);
  xor xor_8 (i21_star, in_1[6], rom_1_data[6]);
  xor xor_9 (i12_star, in_1[15], rom_1_data[15]);
  xor xor_10 (i13_star, in_1[14], rom_1_data[14]);
  xor xor_11 (i14_star, in_1[13], rom_1_data[13]);
  xor xor_12 (i15_star, in_1[12], rom_1_data[12]);
  xor xor_13 (i16_star, in_1[11], rom_1_data[11]);
  xor xor_14 (i17_star, in_1[10], rom_1_data[10]);
  xor xor_15 (i18_star, in_1[9], rom_1_data[9]);
  xor xor_16 (i19_star, in_1[8], rom_1_data[8]);
  xor xor_17 (i4_star, in_1[23], rom_1_data[23]);
  xor xor_18 (i5_star, in_1[22], rom_1_data[22]);
  xor xor_19 (i6_star, in_1[21], rom_1_data[21]);
  xor xor_20 (i7_star, in_1[20], rom_1_data[20]);
  xor xor_21 (i8_star, in_1[19], rom_1_data[19]);
  xor xor_22 (i9_star, in_1[18], rom_1_data[18]);
  xor xor_23 (i10_star, in_1[17], rom_1_data[17]);
  xor xor_24 (i11_star, in_1[16], rom_1_data[16]);
  xor xor_25 (i1_star, in_1[26], rom_1_data[26]);
  xor xor_26 (i2_star, in_1[25], rom_1_data[25]);
  xor xor_27 (i3_star, in_1[24], rom_1_data[24]);

  // Notes on the sheet:
  //   contents of rom_1 (hex, n*v repeats v):
  //   0 1 2 3 4 5 6 7 8 1000000 200000 8000 40000 40 1000 200 10 80 2000000 80000 400000 400 10000 2000 18
  //   3000 600 3000000 c0 18000 600000 c0000 20 800 100 800000 4000000 4000 100000 20000 28 a00000 140000
  //   5000 28000 5000000 a00 140 30 30000 6000 180 c00 180000 6000000 c00000 38 1c0000 38000 e00 7000
  //   e00000 1c0 7000000
endmodule
