// Logisim project pract3.circ as structural Verilog: 1 circuit, main circuit Генератор элементов двоичного поля Галуа
module \Генератор_элементов_двоичного_поля_Галуа  (
);

  wire clock_1_out, register_1_q, register_2_q, register_3_q, register_4_q, register_5_q, xor_1_out;

  Clock clock_1 (.out(clock_1_out));
  Register #(.width(1)) register_1 (.D(register_5_q), .Q(register_1_q), .clk(clock_1_out));  // open: en, clr
  Register #(.width(1)) register_2 (.D(register_1_q), .Q(register_2_q), .clk(clock_1_out));  // open: en, clr
  LED led_1 (.in(register_1_q));
  LED led_2 (.in(register_2_q));
  Register #(.width(1)) register_3 (.D(register_2_q), .Q(register_3_q), .clk(clock_1_out));  // open: en, clr
  LED led_3 (.in(register_3_q));
  xor xor_1 (xor_1_out, register_5_q, register_3_q);
  Register #(.width(1)) register_4 (.D(xor_1_out), .Q(register_4_q), .clk(clock_1_out));  // open: en, clr
  LED led_4 (.in(register_4_q));
  Register #(.width(1)) register_5 (.D(register_4_q), .Q(register_5_q), .clk(clock_1_out));  // open: en, clr
  LED led_5 (.in(register_5_q));

  // Notes on the sheet:
  //   1
  //   0
  //   x
  //   3
  //   x
  //   1
  //   x
  //   2
  //   x
  //   x
  //   x
  //   3
  //   5
  //   4
  //   x
  //   Выполнили
  //   ст.гр.961401
  //   Савченко Е.А.
  //   Перминова А.В.
  //   Матошко М.П.
  //   Савич О.А.
  //   *нами был выбран данный неприводимый многочлен
  //   P(x)= 1+x^3+x^5
endmodule
