// Logisim project LR_4.circ as structural Verilog: 13 circuits, main circuit Структурная схема кодека
module \Структурная_схема_кодека  (
  input  i11,
  input  i10,
  input  i9,
  input  i8,
  input  i7,
  input  i6,
  input  i5,
  input  i4,
  input  i3,
  input  i2,
  input  i1,
  input  e15,
  input  e14,
  input  e13,
  input  e12,
  input  e11,
  input  e10,
  input  e9,
  input  e8,
  input  e7,
  input  e6,
  input  e5,
  input  e4,
  input  e3,
  input  e2,
  input  e1,
  input  \Старт ,
  input  \Старт_2 ,
  input  \Старт_3 ,
  output \с15 ,
  output \с14 ,
  output \с13 ,
  output \с12 ,
  output c11,
  output \с10 ,
  output \с9 ,
  output \с8 ,
  output \с7 ,
  output \с6 ,
  output \с5 ,
  output \с4 ,
  output \с3 ,
  output \с2 ,
  output \с1 ,
  output \с15_2 ,
  output \с14_2 ,
  output \с13_2 ,
  output \с12_2 ,
  output c11_2,
  output \с10_2 ,
  output \с9_2 ,
  output \с8_2 ,
  output \с7_2 ,
  output \с6_2 ,
  output \с5_2 ,
  output \с4_2 ,
  output \с3_2 ,
  output \с2_2 ,
  output \с1_2 ,
  output \с15_3 ,
  output \с14_3 ,
  output \с13_3 ,
  output \с12_3 ,
  output c11_3,
  output \с10_3 ,
  output \с9_3 ,
  output \с8_3 ,
  output \с7_3 ,
  output \с6_3 ,
  output \с5_3 ,
  output \с4_3 ,
  output \с3_3 ,
  output \с2_3 ,
  output \с1_3 ,
  output \с14_star ,
  output \с13_star ,
  output \с12_star ,
  output \с11_star ,
  output \с10_star ,
  output out_80,
  output \с9_star ,
  output \с8_star ,
  output \с7_star ,
  output \с6_star ,
  output \с5_star ,
  output \с4_star ,
  output \с3_star ,
  output \с2_star ,
  output \с1_star ,
  output i11_2,
  output i10_2,
  output i9_2,
  output i8_2,
  output i7_2,
  output i6_2,
  output i5_2,
  output i4_2,
  output i3_2,
  output i2_2,
  output i1_2
);

  wire \функциональная_схема_входа_канала_1_out_37 , \функциональная_схема_входа_канала_1_выход ,
       \функциональная_схема_входа_канала_1_такты_канала , \функциональная_схема_выхода_канала_1_выход ,
       \функциональная_схема_декодера_1_старт_2 , \функциональная_схема_декодера_1_такты ,
       \функциональная_схема_кодера_полный_1_out_31 , \функциональная_схема_кодера_полный_1_выход ,
       \функциональная_схема_кодера_полный_1_такты_кодера ;
  wire [3:0] \функциональная_схема_входа_канала_1_out_36 , \функциональная_схема_кодера_полный_1_out_30 ;

  Hex_Digit_Display hex_digit_display_1 (
    .value(\функциональная_схема_кодера_полный_1_out_30 ), .dp(\функциональная_схема_кодера_полный_1_out_31 ));
  \Функциональная_схема_декодера  \u_функциональная_схема_декодера_1  (
    .\Старт (\Старт_3 ), .\Старт_2 (\функциональная_схема_декодера_1_старт_2 ),
    .\Такты (\функциональная_схема_декодера_1_такты ), .\с15 (\с15_3 ), .\с14 (\с14_3 ), .\с13 (\с13_3 ),
    .\с12 (\с12_3 ), .\с11 (c11_3), .\с10 (\с10_3 ), .\с9 (\с9_3 ), .\с8 (\с8_3 ), .\с7 (\с7_3 ),
    .i5_star(i5_2), .i4_star(i4_2), .i3_star(i3_2), .i2_star(i2_2), .i1_star(i1_2),
    .\Вход (\функциональная_схема_выхода_канала_1_выход ), .\с6 (\с6_3 ), .\с5 (\с5_3 ), .\с4 (\с4_3 ),
    .\с3 (\с3_3 ), .\с2 (\с2_3 ), .\с1 (\с1_3 ), .i10_star(i10_2), .i9_star(i9_2), .i8_star(i8_2),
    .i7_star(i7_2), .i6_star(i6_2), .i11_star(i11_2));
  \Функциональная_схема_кодера__полный  \u_функциональная_схема_кодера_полный_1  (
    .\Старт (\Старт ), .\Выход (\функциональная_схема_кодера_полный_1_выход ),
    .\Такты_кодера (\функциональная_схема_кодера_полный_1_такты_кодера ),
    .out_30(\функциональная_схема_кодера_полный_1_out_30 ),
    .out_31(\функциональная_схема_кодера_полный_1_out_31 ), .i5(i5), .i4(i4), .i3(i3), .i2(i2), .i1(i1),
    .i10(i10), .i9(i9), .i8(i8), .i7(i7), .i6(i6), .i11(i11), .\с9 (\с9 ), .\с8 (\с8 ), .\с7 (\с7 ),
    .\с6 (\с6 ), .\с5 (\с5 ), .\с4 (\с4 ), .\с3 (\с3 ), .\с2 (\с2 ), .\с1 (\с1 ), .\с15 (\с15 ),
    .\с14 (\с14 ), .\с13 (\с13 ), .\с12 (\с12 ), .c11(c11), .\с10 (\с10 ));
  \Функциональная_схема_выхода_канала  \u_функциональная_схема_выхода_канала_1  (
    .\Вход (\функциональная_схема_входа_канала_1_выход ),
    .\Такты_кодера (\функциональная_схема_входа_канала_1_такты_канала ),
    .\Старт (\функциональная_схема_декодера_1_старт_2 ),
    .\Такты_декодера (\функциональная_схема_декодера_1_такты ),
    .\Выход (\функциональная_схема_выхода_канала_1_выход ), .\с10_star (\с9_star ), .\с9_star (\с8_star ),
    .\с8_star (\с7_star ), .\с7_star (\с6_star ), .\с6_star (\с5_star ), .\с5_star (\с4_star ),
    .\с4_star (\с3_star ), .\с3_star (\с2_star ), .\с2_star (\с1_star ), .\с15_star (\с14_star ),
    .\с14_star (\с13_star ), .\с13_star (\с12_star ), .out_8(\с11_star ), .\с12_star (\с10_star ),
    .\с11_star (out_80));
  \Функциональная_схема_входа_канала  \u_функциональная_схема_входа_канала_1  (
    .\Вход (\функциональная_схема_кодера_полный_1_выход ),
    .\Такты_кодера (\функциональная_схема_кодера_полный_1_такты_кодера ), .\Старт (\Старт_2 ),
    .\Выход (\функциональная_схема_входа_канала_1_выход ),
    .\Такты_канала (\функциональная_схема_входа_канала_1_такты_канала ),
    .out_36(\функциональная_схема_входа_канала_1_out_36 ),
    .out_37(\функциональная_схема_входа_канала_1_out_37 ), .e15(e15), .e14(e14), .e13(e13), .e12(e12),
    .e11(e11), .e10(e10), .e9(e9), .e8(e8), .e7(e7), .\с15 (\с15_2 ), .\с14 (\с14_2 ), .\с13 (\с13_2 ),
    .\с12 (\с12_2 ), .c11(c11_2), .\с10 (\с10_2 ), .\с9 (\с9_2 ), .\с8 (\с8_2 ), .\с7 (\с7_2 ),
    .\с6 (\с6_2 ), .\с5 (\с5_2 ), .\с4 (\с4_2 ), .\с3 (\с3_2 ), .\с2 (\с2_2 ), .\с1 (\с1_2 ), .e6(e6),
    .e5(e5), .e4(e4), .e3(e3), .e2(e2), .e1(e1));
  Hex_Digit_Display hex_digit_display_2 (
    .value(\функциональная_схема_входа_канала_1_out_36 ), .dp(\функциональная_схема_входа_канала_1_out_37 ));

  // Notes on the sheet:
  //   с15*
  //   Выполнили
  //   ст.гр,961401
  //   Савченко Е.А
  //   Савич О.А
  //   Перминова А.В.
  //   Матошко М.П.
endmodule

module \Функциональная_схема_кодера__полный  (
  input  i11,
  input  i10,
  input  i9,
  input  i8,
  input  i7,
  input  i6,
  input  i5,
  input  i4,
  input  i3,
  input  i2,
  input  i1,
  input  \Старт ,
  output \Выход ,
  output \с15 ,
  output \с14 ,
  output \с13 ,
  output \с12 ,
  output c11,
  output \с10 ,
  output \с9 ,
  output \с8 ,
  output \с7 ,
  output \с6 ,
  output \с5 ,
  output \с4 ,
  output \с3 ,
  output \с2 ,
  output \с1 ,
  output \Такты_кодера ,
  output [3:0] out_30,
  output out_31
);

  wire or_1_out, shift_register_1_out, \функциональная_схема_генератора_кодер_1_out_4 ;

  Shift_Register #(.length(11)) shift_register_1 (
    .clk(or_1_out), .out(shift_register_1_out), .load(\Старт ), .d0(i11), .d1(i10), .d2(i9), .d3(i8),
    .d4(i7), .d5(i6), .d6(i5), .d7(i4), .d8(i3), .d9(i2), .d10(i1));  // open: shift, in, clr, q0, q1, q2, q3, q4, q5, q6, q7, q8, q9, q10
  or or_1 (or_1_out, \Старт , \Такты_кодера );
  Shift_Register #(.length(15)) shift_register_2 (
    .in(\Выход ), .clk(\Такты_кодера ), .q0(\с15 ), .q1(\с14 ), .q2(\с13 ), .q3(\с12 ), .q4(c11), .q5(\с10 ),
    .q6(\с9 ), .q7(\с8 ), .q8(\с7 ), .q9(\с6 ), .q10(\с5 ), .q11(\с4 ), .q12(\с3 ), .q13(\с2 ), .q14(\с1 ));  // open: shift, out, load, clr, d0, d1, d2, d3, d4, d5, d6, d7, d8, d9, d10, d11, d12, d13, d14
  \Функциональная_схема_кодера__неполный  \u_функциональная_схема_кодера_неполный_1  (
    .\Вход (shift_register_1_out), .\Такты (\Такты_кодера ), .\Выход (\Выход ),
    .in_1(\функциональная_схема_генератора_кодер_1_out_4 ));
  \Функциональная_схема_генератора__кодер  \u_функциональная_схема_генератора_кодер_1  (
    .\Старт (\Старт ), .out_2(out_30), .out_3(out_31),
    .out_4(\функциональная_схема_генератора_кодер_1_out_4 ), .\Такты (\Такты_кодера ));

  // Notes on the sheet:
  //   Информационный вектор
  //   Буфер
  //   Кодер
  //   Генератор (кодера)
  //   Буфер
  //   Индикатор окончания работы кодера
  //   Цифровой индикаатор тактов
endmodule

module \Функциональная_схема_входа_канала  (
  input  \Вход ,
  input  \Такты_кодера ,
  input  e15,
  input  e14,
  input  e13,
  input  e12,
  input  e11,
  input  e10,
  input  e9,
  input  e8,
  input  e7,
  input  e6,
  input  e5,
  input  e4,
  input  e3,
  input  e2,
  input  e1,
  input  \Старт ,
  output \с15 ,
  output \с14 ,
  output \с13 ,
  output \с12 ,
  output c11,
  output \с10 ,
  output \с9 ,
  output \с8 ,
  output \с7 ,
  output \с6 ,
  output \с5 ,
  output \с4 ,
  output \с3 ,
  output \с2 ,
  output \с1 ,
  output \Выход ,
  output \Такты_канала ,
  output [3:0] out_36,
  output out_37
);

  wire or_1_out, or_2_out, shift_register_2_out, shift_register_3_out;

  Shift_Register #(.length(15)) shift_register_1 (
    .in(\Вход ), .clk(\Такты_кодера ), .q0(\с15 ), .q1(\с14 ), .q2(\с13 ), .q3(\с12 ), .q4(c11), .q5(\с10 ),
    .q6(\с9 ), .q7(\с8 ), .q8(\с7 ), .q9(\с6 ), .q10(\с5 ), .q11(\с4 ), .q12(\с3 ), .q13(\с2 ), .q14(\с1 ));  // open: shift, out, load, clr, d0, d1, d2, d3, d4, d5, d6, d7, d8, d9, d10, d11, d12, d13, d14
  Shift_Register #(.length(15)) shift_register_2 (
    .in(\Вход ), .clk(or_1_out), .out(shift_register_2_out), .load(\Старт ), .d0(\с15 ), .d1(\с14 ),
    .d2(\с13 ), .d3(\с12 ), .d4(c11), .d5(\с10 ), .d6(\с9 ), .d7(\с8 ), .d8(\с7 ), .d9(\с6 ), .d10(\с5 ),
    .d11(\с4 ), .d12(\с3 ), .d13(\с2 ), .d14(\с1 ));  // open: shift, clr, q0, q1, q2, q3, q4, q5, q6, q7, q8, q9, q10, q11, q12, q13, q14
  or or_1 (or_1_out, \Старт , \Такты_канала );
  Shift_Register #(.length(15)) shift_register_3 (
    .clk(or_2_out), .out(shift_register_3_out), .load(\Старт ), .d0(e15), .d1(e14), .d2(e13), .d3(e12),
    .d4(e11), .d5(e10), .d6(e9), .d7(e8), .d8(e7), .d9(e6), .d10(e5), .d11(e4), .d12(e3), .d13(e2), .d14(e1));  // open: shift, in, clr, q0, q1, q2, q3, q4, q5, q6, q7, q8, q9, q10, q11, q12, q13, q14
  or or_2 (or_2_out, \Старт , \Такты_канала );
  \Функциональная_схема_генератора__кодер  \u_функциональная_схема_генератора_кодер_1  (
    .\Старт (\Старт ), .out_2(out_36), .out_3(out_37), .\Такты (\Такты_канала ));  // open: out_4
  xor xor_1 (\Выход , shift_register_2_out, shift_register_3_out);

  // Notes on the sheet:
  //   Генератор (канала)
  //   Индикатор окончания работы
  //   Цифровой индикатор тактов
endmodule

module \Функциональная_схема_выхода_канала  (
  input  \Вход ,
  input  \Такты_кодера ,
  input  \Старт ,
  input  \Такты_декодера ,
  output \с15_star ,
  output \с14_star ,
  output \с13_star ,
  output out_8,
  output \с12_star ,
  output \с11_star ,
  output \с10_star ,
  output \с9_star ,
  output \с8_star ,
  output \с7_star ,
  output \с6_star ,
  output \с5_star ,
  output \с4_star ,
  output \с3_star ,
  output \с2_star ,
  output \Выход 
);

  wire or_1_out;

  Shift_Register #(.length(15)) shift_register_1 (
    .in(\Вход ), .clk(\Такты_кодера ), .q0(\с15_star ), .q1(\с14_star ), .q2(\с13_star ), .q3(out_8),
    .q4(\с12_star ), .q5(\с11_star ), .q6(\с10_star ), .q7(\с9_star ), .q8(\с8_star ), .q9(\с7_star ),
    .q10(\с6_star ), .q11(\с5_star ), .q12(\с4_star ), .q13(\с3_star ), .q14(\с2_star ));  // open: shift, out, load, clr, d0, d1, d2, d3, d4, d5, d6, d7, d8, d9, d10, d11, d12, d13, d14
  Shift_Register #(.length(15)) shift_register_2 (
    .clk(or_1_out), .out(\Выход ), .load(\Старт ), .d0(\с15_star ), .d1(\с14_star ), .d2(\с13_star ),
    .d3(out_8), .d4(\с12_star ), .d5(\с11_star ), .d6(\с10_star ), .d7(\с9_star ), .d8(\с8_star ),
    .d9(\с7_star ), .d10(\с6_star ), .d11(\с5_star ), .d12(\с4_star ), .d13(\с3_star ), .d14(\с2_star ));  // open: shift, in, clr, q0, q1, q2, q3, q4, q5, q6, q7, q8, q9, q10, q11, q12, q13, q14
  or or_1 (or_1_out, \Старт , \Такты_декодера );

  // Notes on the sheet:
  //   с1*
endmodule

module \Функциональная_схема_декодера  (
  input  \Вход ,
  input  \Старт ,
  output \с15 ,
  output \с14 ,
  output \с13 ,
  output \с12 ,
  output \с11 ,
  output \с10 ,
  output \с9 ,
  output \с8 ,
  output \с7 ,
  output \с6 ,
  output \с5 ,
  output \с4 ,
  output \с3 ,
  output \с2 ,
  output \с1 ,
  output i11_star,
  output i10_star,
  output i9_star,
  output i8_star,
  output i7_star,
  output i6_star,
  output i5_star,
  output i4_star,
  output i3_star,
  output i2_star,
  output i1_star,
  output \Старт_2 ,
  output \Такты 
);

  wire and_1_out, and_2_out, register_1_q, register_2_q, register_3_q, register_4_q, shift_register_1_out,
       xor_1_out, xor_2_out, xor_3_out, \функциональная_схема_генератора_декодер_1_out_2 ,
       \функциональная_схема_ключа_3_1_выход , \функциональная_схема_ключа_4_1_выход ;

  Shift_Register #(.length(15)) shift_register_1 (
    .in(\Вход ), .clk(\Такты ), .out(shift_register_1_out));  // open: shift, load, clr, d0, q0, d1, q1, d2, q2, d3, q3, d4, q4, d5, q5, d6, q6, d7, q7, d8, q8, d9, q9, d10, q10, d11, q11, d12, q12, d13, q13, d14, q14
  Register #(.width(1)) register_1 (.D(xor_2_out), .Q(register_1_q), .clk(\Такты ));  // open: en, clr
  \Функциональная_схема_генератора__декодер  \u_функциональная_схема_генератора_декодер_1  (
    .\Старт (\Старт ), .out_2(\функциональная_схема_генератора_декодер_1_out_2 ), .\Такты (\Такты ));
  xor xor_1 (xor_1_out, xor_2_out, register_1_q);
  xor xor_2 (xor_2_out, \функциональная_схема_ключа_4_1_выход , \функциональная_схема_ключа_3_1_выход , register_4_q);
  Register #(.width(1)) register_2 (.D(register_3_q), .Q(register_2_q), .clk(\Такты ));  // open: en, clr
  Register #(.width(1)) register_3 (.D(xor_1_out), .Q(register_3_q), .clk(\Такты ));  // open: en, clr
  \Функциональная_схема_ключа_4  \u_функциональная_схема_ключа_4_1  (
    .\Управление (\функциональная_схема_генератора_декодер_1_out_2 ), .\Вход (\Вход ),
    .\Выход (\функциональная_схема_ключа_4_1_выход ));
  Register #(.width(1)) register_4 (.D(register_2_q), .Q(register_4_q), .clk(\Такты ));  // open: en, clr
  \Функциональная_схема_ключа_3  \u_функциональная_схема_ключа_3_1  (
    .\Выход (\функциональная_схема_ключа_3_1_выход ), .\Вход (and_1_out),
    .\Управление (\функциональная_схема_генератора_декодер_1_out_2 ));
  and and_1 (and_1_out, register_4_q, ~register_2_q, ~register_3_q, ~register_1_q);  // AND_Gate
  Shift_Register #(.length(15)) shift_register_2 (
    .in(xor_3_out), .clk(and_2_out), .q0(\с15 ), .q1(\с14 ), .q2(\с13 ), .q3(\с12 ), .q4(i11_star),
    .q5(i10_star), .q6(i9_star), .q7(i8_star), .q8(i7_star), .q9(i6_star), .q10(i5_star), .q11(i4_star),
    .q12(i3_star), .q13(i2_star), .q14(i1_star));  // open: shift, out, load, clr, d0, d1, d2, d3, d4, d5, d6, d7, d8, d9, d10, d11, d12, d13, d14
  xor xor_3 (xor_3_out, shift_register_1_out, \функциональная_схема_ключа_3_1_выход );
  and and_2 (and_2_out, \Такты , \функциональная_схема_генератора_декодер_1_out_2 );

  assign \с1  = i1_star;
  assign \с2  = i2_star;
  assign \с3  = i3_star;
  assign \с4  = i4_star;
  assign \с5  = i5_star;
  assign \с6  = i6_star;
  assign \с7  = i7_star;
  assign \с8  = i8_star;
  assign \с9  = i9_star;
  assign \с10  = i10_star;
  assign \с11  = i11_star;
  assign \Старт_2  = \Старт ;

  // Notes on the sheet:
  //   Генератор (декодера)
  //   Ключ 1
  //   Ключ 2
  //   Кодовое слово
  //   Информационный вектор
endmodule

module \Функциональная_схема_кодера__неполный  (
  input  in_1,
  input  \Вход ,
  input  \Такты ,
  output \Выход 
);

  wire register_1_q, register_2_q, register_3_q, register_4_q, xor_1_out, xor_2_out,
       \функциональная_схема_ключа_1_1_выход ;

  xor xor_1 (xor_1_out, \функциональная_схема_ключа_1_1_выход , register_1_q);
  Register #(.width(1)) register_1 (
    .D(\функциональная_схема_ключа_1_1_выход ), .Q(register_1_q), .clk(\Такты ));  // open: en, clr
  xor xor_2 (xor_2_out, \Вход , register_4_q);
  \Функциональная_схема_ключа_1  \u_функциональная_схема_ключа_1_1  (
    .\Выход (\функциональная_схема_ключа_1_1_выход ), .\Управление (in_1), .\Вход (xor_2_out));
  Register #(.width(1)) register_2 (.D(xor_1_out), .Q(register_2_q), .clk(\Такты ));  // open: en, clr
  Register #(.width(1)) register_3 (.D(register_2_q), .Q(register_3_q), .clk(\Такты ));  // open: en, clr
  Register #(.width(1)) register_4 (.D(register_3_q), .Q(register_4_q), .clk(\Такты ));  // open: en, clr
  \Функциональная_схема_ключа_2  \u_функциональная_схема_ключа_2_1  (
    .\Вход_1 (\Вход ), .\Управление (in_1), .\Вход_2 (register_4_q), .\Выход (\Выход ));

  // Notes on the sheet:
  //   Ключ 1
  //   Ключ 2
  //   Управление ключами
endmodule

module \Функциональная_схема_ключа_1  (
  input  \Управление ,
  input  \Вход ,
  output \Выход 
);

  and and_1 (\Выход , ~\Управление , \Вход );  // AND_Gate
endmodule

module \Функциональная_схема_ключа_2  (
  input  \Вход_1 ,
  input  \Управление ,
  input  \Вход_2 ,
  output \Выход 
);

  wire and_1_out, and_2_out;

  and and_1 (and_1_out, \Вход_1 , ~\Управление );  // AND_Gate
  and and_2 (and_2_out, \Управление , \Вход_2 );
  or or_1 (\Выход , and_1_out, and_2_out);
endmodule

module \Функциональная_схема_ключа_3  (
  input  \Вход ,
  input  \Управление ,
  output \Выход 
);

  and and_1 (\Выход , \Вход , \Управление );
endmodule

module \Функциональная_схема_ключа_4  (
  input  \Управление ,
  input  \Вход ,
  output \Выход 
);

  and and_1 (\Выход , ~\Управление , \Вход );  // AND_Gate
endmodule

module \Функциональная_схема_генератора__кодер  (
  input  \Старт ,
  output [3:0] out_2,
  output out_3,
  output out_4,
  output \Такты 
);

  wire and_1_out, and_2_out, d_ff_1_q, d_ff_2_qn, \функциональная_схема_тактового_генератора_1_такты ;

  D_Flip_Flop d_ff_1 (.clk(\Старт ), .D(\Старт ), .Q(d_ff_1_q));  // open: Qn, preset, en, reset
  \Функциональная_схема_тактового_генератора  \u_функциональная_схема_тактового_генератора_1  (
    .\Такты (\функциональная_схема_тактового_генератора_1_такты ), .\Установка_в__0 (\Старт ));
  Counter #(.width(4), .max('hf)) counter_1 (.Q(out_2), .clk(and_1_out), .clr(\Старт ));  // open: load, D, count, carry
  and and_1 (and_1_out, d_ff_1_q, \функциональная_схема_тактового_генератора_1_такты , ~out_3);  // AND_Gate
  and and_2 (and_2_out, out_2[3], ~out_2[2], out_2[1], out_2[0]);  // AND_Gate
  and and_3 (out_3, out_2[3], out_2[2], out_2[1], out_2[0]);
  D_Flip_Flop #(.trigger("falling")) d_ff_2 (
    .clk(\функциональная_схема_тактового_генератора_1_такты ), .D(and_2_out), .Q(out_4), .Qn(d_ff_2_qn),
    .en(d_ff_2_qn), .reset(\Старт ));  // open: preset
  and and_4 (\Такты , d_ff_1_q, ~out_3, ~\Старт , \функциональная_схема_тактового_генератора_1_такты );  // AND_Gate

  // Notes on the sheet:
  //   Счетчик тактов
  //   Блокировка
  //   произвольного
  //   запуска
  //   Генератор (тактовый)
  //   Остановка счета
  //   Остановка счета и подачи тактов при значении 9
  //   Цифровой индикатор тактов
  //   Индикатор окончания работы кодера
  //   Переключение ключей после 5 тактов
endmodule

module \Функциональная_схема_генератора__декодер  (
  input  \Старт ,
  output out_2,
  output \Такты 
);

  wire and_1_out, and_2_out, and_3_out, d_ff_1_q, d_ff_2_qn,
       \функциональная_схема_тактового_генератора_1_такты ;
  wire [4:0] counter_1_q;

  \Функциональная_схема_тактового_генератора  \u_функциональная_схема_тактового_генератора_1  (
    .\Такты (\функциональная_схема_тактового_генератора_1_такты ), .\Установка_в__0 (\Старт ));
  Counter #(.width(5), .max('h1f)) counter_1 (
    .Q(counter_1_q), .clk(and_1_out), .clr(\Старт ));  // open: load, D, count, carry
  and and_1 (and_1_out, d_ff_1_q, \функциональная_схема_тактового_генератора_1_такты , ~and_3_out);  // AND_Gate
  D_Flip_Flop d_ff_1 (.clk(\Старт ), .D(\Старт ), .Q(d_ff_1_q));  // open: Qn, preset, en, reset
  and and_2 (and_2_out, counter_1_q[3], counter_1_q[2], counter_1_q[1], counter_1_q[0]);
  and and_3 (and_3_out, ~counter_1_q[0], counter_1_q[1], counter_1_q[2], counter_1_q[3], counter_1_q[4]);  // AND_Gate
  D_Flip_Flop #(.trigger("falling")) d_ff_2 (
    .clk(\функциональная_схема_тактового_генератора_1_такты ), .D(and_2_out), .Q(out_2), .Qn(d_ff_2_qn),
    .en(d_ff_2_qn), .reset(\Старт ));  // open: preset
  and and_4 (\Такты , d_ff_1_q, ~and_3_out, ~\Старт , \функциональная_схема_тактового_генератора_1_такты );  // AND_Gate

  // Notes on the sheet:
  //   Блокировка
  //   произвольного
  //   запуска
  //   Генератор (тактовый)
  //   Счетчик тактов
  //   Остановка счета
  //   Остановка счета и подачи тактов при значении 30
  //   Переключение ключей после 15 тактов
endmodule

module \Функциональная_схема_тактового_генератора  (
  input  \Установка_в__0 ,
  output \Такты 
);

  wire clock_1_out, d_ff_1_q, d_ff_1_qn, d_ff_2_q, d_ff_2_qn;

  Clock clock_1 (.out(clock_1_out));
  D_Flip_Flop d_ff_1 (
    .clk(clock_1_out), .D(d_ff_1_qn), .Q(d_ff_1_q), .Qn(d_ff_1_qn), .reset(\Установка_в__0 ));  // open: preset, en
  D_Flip_Flop #(.trigger("falling")) d_ff_2 (
    .clk(clock_1_out), .D(d_ff_2_qn), .Q(d_ff_2_q), .Qn(d_ff_2_qn), .reset(\Установка_в__0 ));  // open: preset, en
  xor xor_1 (\Такты , d_ff_1_q, d_ff_2_q);
endmodule
