// Logisim project PTK1_2.circ as structural Verilog: 4 circuits, main circuit Структурная схема кодека
module \Структурная_схема_кодека  (
  input  i1,
  input  e1,
  input  i2,
  input  e2,
  input  i3,
  input  e3,
  input  i4,
  input  e4,
  input  i5,
  input  e5,
  input  i6,
  input  e6,
  input  i7,
  input  e7,
  input  i8,
  input  e8,
  input  i9,
  input  e9,
  input  i10,
  input  e10,
  input  i11,
  input  e11,
  input  e12,
  input  e13,
  input  e14,
  input  e15,
  output out_27,
  output \с1_star ,
  output i1_star,
  output out_30,
  output \с2_star ,
  output i2_star,
  output out_33,
  output \с3_star ,
  output i3_star,
  output \с5 ,
  output \с4_star ,
  output i4_star,
  output \с6 ,
  output \с5_star ,
  output i5_star,
  output \с7 ,
  output \с6_star ,
  output i6_star,
  output \с8 ,
  output \с7_star ,
  output i7_star,
  output \с9 ,
  output \с8_star ,
  output i8_star,
  output out_51,
  output \с9_star ,
  output i9_star,
  output \с10 ,
  output \с10_star ,
  output i10_star,
  output \с11 ,
  output \с11_star ,
  output i11_star,
  output \с12 ,
  output \с12_star ,
  output \с13 ,
  output \с13_star ,
  output \с14 ,
  output \с14_star ,
  output \с15 ,
  output \с15_star 
);

  wire \функциональная_схема_синдромного_декодера_1_s1 , \функциональная_схема_синдромного_декодера_1_s2 ,
       \функциональная_схема_синдромного_декодера_1_s3 , \функциональная_схема_синдромного_декодера_1_s4 ;
  wire [14:0] \функциональная_схема_канала_1_out_32 , \функциональная_схема_кодера_1_out_27 ;

  \Функциональная_схема_кодера  \u_функциональная_схема_кодера_1  (
    .i1(i1), .i2(i2), .i3(i3), .i4(i4), .i5(i5), .i6(i6), .i7(i7), .i8(i8), .i9(i9), .i10(i10), .i11(i11),
    .c1(out_27), .c2(out_30), .c3(out_33), .c4(\с5 ), .c5(\с6 ), .c6(\с7 ), .c7(\с8 ), .c8(\с9 ),
    .c9(out_51), .c10(\с10 ), .c11(\с11 ), .c12(\с12 ), .c13(\с13 ), .c14(\с14 ), .c15(\с15 ),
    .out_27(\функциональная_схема_кодера_1_out_27 ));
  \Функциональная_схема_канала  \u_функциональная_схема_канала_1  (
    .e1(e1), .e2(e2), .e3(e3), .e4(e4), .e5(e5), .e6(e6), .e7(e7), .e8(e8), .e9(e9), .e10(e10), .e11(e11),
    .e12(e12), .e13(e13), .e14(e14), .e15(e15), .in_16(\функциональная_схема_кодера_1_out_27 ),
    .c1_star(\с1_star ), .c2_star(\с2_star ), .c3_star(\с3_star ), .c4_star(\с4_star ), .c5_star(\с5_star ),
    .c6_star(\с6_star ), .c7_star(\с7_star ), .c1_star_2(\с8_star ), .c2_star_2(\с9_star ),
    .c3_star_2(\с10_star ), .c4_star_2(\с11_star ), .c5_star_2(\с12_star ), .c6_star_2(\с13_star ),
    .c7_star_2(\с14_star ), .c7_star_3(\с15_star ), .out_32(\функциональная_схема_канала_1_out_32 ));
  \Функциональная_схема_синдромного_декодера  \u_функциональная_схема_синдромного_декодера_1  (
    .in_1(\функциональная_схема_канала_1_out_32 ), .i1_star(i1_star), .i2_star(i2_star), .i3_star(i3_star),
    .i4_star(i4_star), .i5_star(i5_star), .i6_star(i6_star), .i7_star(i7_star), .i8_star(i8_star),
    .i9_star(i9_star), .i10_star(i10_star), .i11_star(i11_star),
    .s1(\функциональная_схема_синдромного_декодера_1_s1 ),
    .s2(\функциональная_схема_синдромного_декодера_1_s2 ),
    .s3(\функциональная_схема_синдромного_декодера_1_s3 ),
    .s4(\функциональная_схема_синдромного_декодера_1_s4 ));
  LED led_1 (.in(\функциональная_схема_синдромного_декодера_1_s4 ));
  LED led_2 (.in(\функциональная_схема_синдромного_декодера_1_s3 ));
  LED led_3 (.in(\функциональная_схема_синдромного_декодера_1_s2 ));
  LED led_4 (.in(\функциональная_схема_синдромного_декодера_1_s1 ));

  // Notes on the sheet:
  //   КОДЕР
  //   Синдромный кодек кода
  //   КАНАЛ
  //   ДЕКОДЕР
  //   s1
  //   s2
  //   s3
  //   s4
  //   Савич О.А.
  //   Исходные данные:
  //   n=15 длина кода
  //   d=3 кодовое расстояние
  //   Перминова А.В.
  //   Савченко Е.А.
  //   Матошко М.П.
  //   k=11 количество информационых разрядов
  //   r=4 количество проверочных разрядов
  //   t=1 кратность исправляемых ошибок
  //   Выполнили студенты гр. 961401:
endmodule

module \Функциональная_схема_кодера  (
  input  i1,
  input  i2,
  input  i3,
  input  i4,
  input  i5,
  input  i6,
  input  i7,
  input  i8,
  input  i9,
  input  i10,
  input  i11,
  output c1,
  output c2,
  output c3,
  output c4,
  output c5,
  output c6,
  output c7,
  output c8,
  output c9,
  output c10,
  output c11,
  output c12,
  output c13,
  output c14,
  output c15,
  output [14:0] out_27
);

  xor xor_1 (c12, i1, i2, i4, i5, i7, i9, i11);
  xor xor_2 (c13, i1, i3, i4, i6, i7, i10, i11);
  xor xor_3 (c14, i2, i3, i4, i8, i9, i10, i11);
  xor xor_4 (c15, i5, i6, i7, i8, i9, i10, i11);

  assign c1 = i1;
  assign c2 = i2;
  assign c3 = i3;
  assign c4 = i4;
  assign c5 = i5;
  assign c6 = i6;
  assign c7 = i7;
  assign c8 = i8;
  assign c9 = i9;
  assign c10 = i10;
  assign c11 = i11;
  assign out_27 = {i1, i2, i3, i4, i5, i6, i7, i8, i9, i10, i11, c12, c13, c14, c15};
endmodule

module \Функциональная_схема_канала  (
  input  e1,
  input  e2,
  input  e3,
  input  e4,
  input  e5,
  input  e6,
  input  e7,
  input  e8,
  input  e9,
  input  e10,
  input  e11,
  input  e12,
  input  e13,
  input  e14,
  input  e15,
  input  [14:0] in_16,
  output c1_star,
  output c2_star,
  output c3_star,
  output c4_star,
  output c5_star,
  output c6_star,
  output c7_star,
  output c1_star_2,
  output c2_star_2,
  output c3_star_2,
  output c4_star_2,
  output c5_star_2,
  output c6_star_2,
  output c7_star_2,
  output c7_star_3,
  output [14:0] out_32
);

  xor xor_1 (c7_star_2, e14, in_16[1]);
  xor xor_2 (c7_star_3, e15, in_16[0]);
  xor xor_3 (c3_star_2, e10, in_16[5]);
  xor xor_4 (c4_star_2, e11, in_16[4]);
  xor xor_5 (c5_star_2, e12, in_16[3]);
  xor xor_6 (c6_star_2, e13, in_16[2]);
  xor xor_7 (c6_star, e6, in_16[9]);
  xor xor_8 (c7_star, e7, in_16[8]);
  xor xor_9 (c1_star_2, e8, in_16[7]);
  xor xor_10 (c2_star_2, e9, in_16[6]);
  xor xor_11 (c2_star, e2, in_16[13]);
  xor xor_12 (c3_star, e3, in_16[12]);
  xor xor_13 (c4_star, e4, in_16[11]);
  xor xor_14 (c5_star, e5, in_16[10]);
  xor xor_15 (c1_star, e1, in_16[14]);

  assign out_32 = {c1_star, c2_star, c3_star, c4_star, c5_star, c6_star, c7_star, c1_star_2, c2_star_2, c3_star_2, c4_star_2, c5_star_2, c6_star_2, c7_star_2, c7_star_3};
endmodule

module \Функциональная_схема_синдромного_декодера  (
  input  [14:0] in_1,
  output i1_star,
  output i2_star,
  output i3_star,
  output i4_star,
  output i5_star,
  output i6_star,
  output i7_star,
  output i8_star,
  output i9_star,
  output i10_star,
  output i11_star,
  output s1,
  output s2,
  output s3,
  output s4
);

  wire and_1_out, and_2_out, and_3_out, and_4_out, and_5_out, and_6_out, and_7_out, and_8_out, and_9_out,
       and_10_out, and_11_out, not_1_out, not_2_out, not_3_out, not_4_out, not_5_out, not_6_out, not_7_out,
       not_8_out, not_9_out, not_10_out, not_11_out, not_12_out, not_13_out, not_14_out, not_15_out,
       not_16_out;

  xor xor_1 (s1, in_1[14], in_1[13], in_1[11], in_1[10], in_1[8], in_1[6], in_1[4], in_1[3]);
  xor xor_2 (s2, in_1[14], in_1[12], in_1[11], in_1[9], in_1[8], in_1[5], in_1[4], in_1[2]);
  xor xor_3 (s3, in_1[13], in_1[12], in_1[11], in_1[7], in_1[6], in_1[5], in_1[4], in_1[1]);
  xor xor_4 (s4, in_1[10], in_1[9], in_1[8], in_1[7], in_1[6], in_1[5], in_1[4], in_1[0]);
  not not_1 (not_1_out, s3);
  not not_2 (not_2_out, s4);
  not not_3 (not_3_out, s2);
  not not_4 (not_4_out, s4);
  not not_5 (not_5_out, s1);
  not not_6 (not_6_out, s4);
  not not_7 (not_7_out, s4);
  not not_8 (not_8_out, s2);
  not not_9 (not_9_out, s3);
  not not_10 (not_10_out, s1);
  not not_11 (not_11_out, s3);
  not not_12 (not_12_out, s3);
  not not_13 (not_13_out, s1);
  not not_14 (not_14_out, s2);
  not not_15 (not_15_out, s2);
  not not_16 (not_16_out, s1);
  and and_1 (and_1_out, s1, s2, not_1_out, not_2_out);
  and and_2 (and_2_out, s1, not_3_out, s3, not_4_out);
  and and_3 (and_3_out, not_5_out, s2, s3, not_6_out);
  and and_4 (and_4_out, s1, s2, s3, not_7_out);
  and and_5 (and_5_out, s1, not_8_out, not_9_out, s4);
  and and_6 (and_6_out, not_10_out, s2, not_11_out, s4);
  and and_7 (and_7_out, s1, s2, not_12_out, s4);
  and and_8 (and_8_out, not_13_out, not_14_out, s3, s4);
  and and_9 (and_9_out, s1, not_15_out, s3, s4);
  and and_10 (and_10_out, not_16_out, s2, s3, s4);
  and and_11 (and_11_out, s1, s2, s3, s4);
  xor xor_5 (i1_star, in_1[14], and_1_out);
  xor xor_6 (i2_star, in_1[13], and_2_out);
  xor xor_7 (i3_star, in_1[12], and_3_out);
  xor xor_8 (i4_star, in_1[11], and_4_out);
  xor xor_9 (i5_star, in_1[10], and_5_out);
  xor xor_10 (i6_star, in_1[9], and_6_out);
  xor xor_11 (i7_star, in_1[8], and_7_out);
  xor xor_12 (i8_star, in_1[7], and_8_out);
  xor xor_13 (i9_star, in_1[6], and_9_out);
  xor xor_14 (i10_star, in_1[5], and_10_out);
  xor xor_15 (i11_star, in_1[4], and_11_out);

  // Notes on the sheet:
  //   БВС
  //   БАС
  //   БК
endmodule
