// Logisim project pract1.circ as structural Verilog: 6 circuits, main circuit Структурная схема кодека
module \Структурная_схема_кодека  (
  input  i1,
  input  e1,
  input  i2,
  input  e2,
  input  i3,
  input  e3,
  input  i4,
  input  e4,
  input  e5,
  input  e6,
  input  e7,
  input  i1_2,
  input  e1_2,
  input  i2_2,
  input  e2_2,
  input  i3_2,
  input  e3_2,
  input  i4_2,
  input  e4_2,
  input  e5_2,
  input  e6_2,
  input  e7_2,
  output c1,
  output c1_star,
  output i1_star,
  output c2,
  output c2_star,
  output i2_star,
  output c3,
  output c3_star,
  output i3_star,
  output c4,
  output c4_star,
  output i4_star,
  output c5,
  output c5_star,
  output c6,
  output c6_star,
  output c7,
  output c7_star,
  output out_41,
  output c1_star_2,
  output c2_2,
  output c2_star_2,
  output c3_2,
  output c3_star_2,
  output c4_2,
  output c4_star_2,
  output out_49,
  output c5_2,
  output c5_star_2,
  output out_52,
  output out_53,
  output c6_2,
  output c6_star_2,
  output out_56,
  output c7_2,
  output c7_star_2
);

  wire \функциональная_схема_синдромного_декодера_1_out_6 ,
       \функциональная_схема_синдромного_декодера_1_out_7 ,
       \функциональная_схема_синдромного_декодера_1_out_8 ;
  wire [6:0] \функциональная_схема_канала_1_out_16 , \функциональная_схема_канала_2_out_16 ,
       \функциональная_схема_кодера_1_out_12 , \функциональная_схема_кодера_2_out_12 ;

  \Функциональная_схема_кодера  \u_функциональная_схема_кодера_1  (
    .i1(i1), .i2(i2), .i3(i3), .i4(i4), .c1(c1), .c2(c2), .c3(c3), .c4(c4),
    .out_12(\функциональная_схема_кодера_1_out_12 ), .c5(c5), .c6(c6), .c7(c7));
  \Функциональная_схема_кодера  \u_функциональная_схема_кодера_2  (
    .i1(i1_2), .i2(i2_2), .i3(i3_2), .i4(i4_2), .c1(out_41), .c2(c2_2), .c3(c3_2), .c4(c4_2),
    .out_12(\функциональная_схема_кодера_2_out_12 ), .c5(c5_2), .c6(c6_2), .c7(c7_2));
  \Функциональная_схема_канала  \u_функциональная_схема_канала_1  (
    .e1(e1), .e2(e2), .e3(e3), .e4(e4), .e5(e5), .e6(e6), .e7(e7),
    .in_8(\функциональная_схема_кодера_1_out_12 ), .c1_star(c1_star), .c2_star(c2_star), .c3_star(c3_star),
    .c4_star(c4_star), .c5_star(c5_star), .c6_star(c6_star), .c7_star(c7_star),
    .out_16(\функциональная_схема_канала_1_out_16 ));
  \Функциональная_схема_канала  \u_функциональная_схема_канала_2  (
    .e1(e1_2), .e2(e2_2), .e3(e3_2), .e4(e4_2), .e5(e5_2), .e6(e6_2), .e7(e7_2),
    .in_8(\функциональная_схема_кодера_2_out_12 ), .c1_star(c1_star_2), .c2_star(c2_star_2),
    .c3_star(c3_star_2), .c4_star(c4_star_2), .c5_star(c5_star_2), .c6_star(c6_star_2), .c7_star(c7_star_2),
    .out_16(\функциональная_схема_канала_2_out_16 ));
  \Функциональная_схема_синдромного_декодера  \u_функциональная_схема_синдромного_декодера_1  (
    .in_1(\функциональная_схема_канала_1_out_16 ), .i1_star(i1_star), .i2_star(i2_star), .i3_star(i3_star),
    .i4_star(i4_star), .out_6(\функциональная_схема_синдромного_декодера_1_out_6 ),
    .out_7(\функциональная_схема_синдромного_декодера_1_out_7 ),
    .out_8(\функциональная_схема_синдромного_декодера_1_out_8 ));
  LED led_1 (.in(\функциональная_схема_синдромного_декодера_1_out_8 ));
  LED led_2 (.in(\функциональная_схема_синдромного_декодера_1_out_7 ));
  LED led_3 (.in(\функциональная_схема_синдромного_декодера_1_out_6 ));
  \Функциональная_схема_мажоритарного_декодера  \u_функциональная_схема_мажоритарного_декодера_1  (
    .in_1(\функциональная_схема_канала_2_out_16 ), .out_2(out_49), .out_3(out_52), .out_4(out_53),
    .out_5(out_56));

  // Notes on the sheet:
  //   Кодер
  //   Кодер
  //   Синдромный кодек 
  //   Канал
  //   Мажоритарный кодек 
  //   Канал
  //   Декодер
  //   Декодер
  //   s1
  //   s2
  //   s3
  //   n=7 длина кода
  //   d=3 кодовое расстояние
  //   k=4 количество информационых разрядов
  //   r=3 количество проверочных разрядов
  //   t=1 кратность исправляемых ошибок
  //   Выполнили
  //   ст.гр. 961401
  //   Савченко Е.А.
  //   Перминова А.В.
  //   Матошко М.П.
  //   Савич О.А.
endmodule

module \Функциональная_схема_кодера  (
  input  i1,
  input  i2,
  input  i3,
  input  i4,
  output c1,
  output c2,
  output c3,
  output c4,
  output c5,
  output c6,
  output c7,
  output [6:0] out_12
);

  xor xor_1 (c5, i1, i2, i4);
  xor xor_2 (c6, i1, i3, i4);
  xor xor_3 (c7, i2, i3, i4);

  assign c1 = i1;
  assign c2 = i2;
  assign c3 = i3;
  assign c4 = i4;
  assign out_12 = {i1, i2, i3, i4, c5, c6, c7};
endmodule

module \Функциональная_схема_канала  (
  input  e1,
  input  e2,
  input  e3,
  input  e4,
  input  e5,
  input  e6,
  input  e7,
  input  [6:0] in_8,
  output c1_star,
  output c2_star,
  output c3_star,
  output c4_star,
  output c5_star,
  output c6_star,
  output c7_star,
  output [6:0] out_16
);

  xor xor_1 (c1_star, e1, in_8[6]);
  xor xor_2 (c2_star, e2, in_8[5]);
  xor xor_3 (c3_star, e3, in_8[4]);
  xor xor_4 (c4_star, e4, in_8[3]);
  xor xor_5 (c5_star, e5, in_8[2]);
  xor xor_6 (c6_star, e6, in_8[1]);
  xor xor_7 (c7_star, e7, in_8[0]);

  assign out_16 = {c1_star, c2_star, c3_star, c4_star, c5_star, c6_star, c7_star};
endmodule

module \Функциональная_схема_синдромного_декодера  (
  input  [6:0] in_1,
  output i1_star,
  output i2_star,
  output i3_star,
  output i4_star,
  output out_6,
  output out_7,
  output out_8
);

  wire and_1_out, and_2_out, and_3_out, and_4_out, not_1_out, not_2_out, not_3_out;

  xor xor_1 (out_6, in_1[6], in_1[5], in_1[3], in_1[2]);
  xor xor_2 (out_8, in_1[5], in_1[4], in_1[3], in_1[0]);
  xor xor_3 (out_7, in_1[6], in_1[4], in_1[3], in_1[1]);
  not not_1 (not_1_out, out_8);
  not not_2 (not_2_out, out_7);
  not not_3 (not_3_out, out_6);
  and and_1 (and_1_out, out_6, out_7, not_1_out);
  and and_2 (and_2_out, out_6, not_2_out, out_8);
  and and_3 (and_3_out, not_3_out, out_7, out_8);
  and and_4 (and_4_out, out_6, out_7, out_8);
  xor xor_4 (i1_star, in_1[6], and_1_out);
  xor xor_5 (i2_star, in_1[5], and_2_out);
  xor xor_6 (i3_star, in_1[4], and_3_out);
  xor xor_7 (i4_star, in_1[3], and_4_out);

  // Notes on the sheet:
  //   s1
  //   БВС
  //   s3
  //   s2
  //   БАС
  //   БК
endmodule

module \Мажоритарный_элемент_на_три_входа  (
  input  a,
  input  b,
  input  c,
  output x
);

  wire and_1_out, and_2_out, and_3_out;

  and and_1 (and_1_out, b, c);
  and and_2 (and_2_out, a, c);
  and and_3 (and_3_out, a, b);
  or or_1 (x, and_1_out, and_2_out, and_3_out);
endmodule

module \Функциональная_схема_мажоритарного_декодера  (
  input  [6:0] in_1,
  output out_2,
  output out_3,
  output out_4,
  output out_5
);

  wire xor_1_out, xor_2_out, xor_3_out, xor_4_out, xor_5_out, xor_6_out, xor_7_out, xor_8_out, xor_9_out,
       xor_10_out, xor_11_out, xor_12_out, xor_13_out, xor_14_out, xor_15_out, xor_16_out, xor_17_out,
       xor_18_out, xor_19_out, xor_20_out, xor_21_out, xor_22_out, xor_23_out, xor_24_out, xor_25_out,
       xor_26_out, xor_27_out, xor_28_out, xor_29_out, xor_30_out, xor_31_out, xor_32_out,
       \мажоритарный_элемент_на_три_входа_1_x , \мажоритарный_элемент_на_три_входа_2_x ,
       \мажоритарный_элемент_на_три_входа_3_x , \мажоритарный_элемент_на_три_входа_4_x ,
       \мажоритарный_элемент_на_три_входа_5_x , \мажоритарный_элемент_на_три_входа_6_x ,
       \мажоритарный_элемент_на_три_входа_7_x , \мажоритарный_элемент_на_три_входа_8_x ;

  xor xor_1 (xor_1_out, in_1[6], in_1[2]);
  xor xor_2 (xor_2_out, in_1[4], in_1[0]);
  xor xor_3 (xor_3_out, in_1[5], in_1[3]);
  xor xor_4 (xor_4_out, in_1[6], in_1[3]);
  xor xor_5 (xor_5_out, in_1[5], in_1[2]);
  xor xor_6 (xor_6_out, in_1[4], in_1[1]);
  xor xor_7 (xor_7_out, in_1[5], in_1[0]);
  xor xor_8 (xor_8_out, in_1[6], in_1[1]);
  xor xor_9 (xor_9_out, in_1[4], in_1[3]);
  xor xor_10 (xor_10_out, in_1[5], in_1[1]);
  xor xor_11 (xor_11_out, in_1[6], in_1[0]);
  xor xor_12 (xor_12_out, in_1[4], in_1[2]);
  xor xor_13 (xor_13_out, in_1[4], in_1[1]);
  xor xor_14 (xor_14_out, in_1[5], in_1[2]);
  xor xor_15 (xor_15_out, in_1[6], in_1[3]);
  xor xor_16 (xor_16_out, in_1[4], in_1[2]);
  xor xor_17 (xor_17_out, in_1[6], in_1[0]);
  xor xor_18 (xor_18_out, in_1[5], in_1[1]);
  xor xor_19 (xor_19_out, in_1[5], in_1[3]);
  xor xor_20 (xor_20_out, in_1[6], in_1[2]);
  xor xor_21 (xor_21_out, in_1[4], in_1[0]);
  xor xor_22 (xor_22_out, in_1[4], in_1[3]);
  xor xor_23 (xor_23_out, in_1[5], in_1[0]);
  xor xor_24 (xor_24_out, in_1[6], in_1[1]);
  \Мажоритарный_элемент_на_три_входа  \u_мажоритарный_элемент_на_три_входа_1  (
    .a(xor_1_out), .b(xor_2_out), .c(xor_3_out), .x(\мажоритарный_элемент_на_три_входа_1_x ));
  \Мажоритарный_элемент_на_три_входа  \u_мажоритарный_элемент_на_три_входа_2  (
    .a(xor_4_out), .b(xor_5_out), .c(xor_6_out), .x(\мажоритарный_элемент_на_три_входа_2_x ));
  \Мажоритарный_элемент_на_три_входа  \u_мажоритарный_элемент_на_три_входа_3  (
    .a(xor_7_out), .b(xor_8_out), .c(xor_9_out), .x(\мажоритарный_элемент_на_три_входа_3_x ));
  \Мажоритарный_элемент_на_три_входа  \u_мажоритарный_элемент_на_три_входа_4  (
    .a(xor_10_out), .b(xor_11_out), .c(xor_12_out), .x(\мажоритарный_элемент_на_три_входа_4_x ));
  \Мажоритарный_элемент_на_три_входа  \u_мажоритарный_элемент_на_три_входа_5  (
    .a(xor_13_out), .b(xor_14_out), .c(xor_15_out), .x(\мажоритарный_элемент_на_три_входа_5_x ));
  \Мажоритарный_элемент_на_три_входа  \u_мажоритарный_элемент_на_три_входа_6  (
    .a(xor_16_out), .b(xor_17_out), .c(xor_18_out), .x(\мажоритарный_элемент_на_три_входа_6_x ));
  \Мажоритарный_элемент_на_три_входа  \u_мажоритарный_элемент_на_три_входа_7  (
    .a(xor_19_out), .b(xor_20_out), .c(xor_21_out), .x(\мажоритарный_элемент_на_три_входа_7_x ));
  \Мажоритарный_элемент_на_три_входа  \u_мажоритарный_элемент_на_три_входа_8  (
    .a(xor_22_out), .b(xor_23_out), .c(xor_24_out), .x(\мажоритарный_элемент_на_три_входа_8_x ));
  xor xor_25 (xor_25_out, \мажоритарный_элемент_на_три_входа_1_x , in_1[2]);
  xor xor_26 (xor_26_out, \мажоритарный_элемент_на_три_входа_2_x , in_1[3]);
  xor xor_27 (xor_27_out, \мажоритарный_элемент_на_три_входа_3_x , in_1[0]);
  xor xor_28 (xor_28_out, \мажоритарный_элемент_на_три_входа_4_x , in_1[1]);
  xor xor_29 (xor_29_out, \мажоритарный_элемент_на_три_входа_5_x , in_1[1]);
  xor xor_30 (xor_30_out, \мажоритарный_элемент_на_три_входа_6_x , in_1[2]);
  xor xor_31 (xor_31_out, \мажоритарный_элемент_на_три_входа_7_x , in_1[5]);
  xor xor_32 (xor_32_out, \мажоритарный_элемент_на_три_входа_8_x , in_1[4]);
  \Мажоритарный_элемент_на_три_входа  \u_мажоритарный_элемент_на_три_входа_9  (
    .a(xor_25_out), .b(xor_26_out), .c(in_1[6]), .x(out_2));
  \Мажоритарный_элемент_на_три_входа  \u_мажоритарный_элемент_на_три_входа_10  (
    .a(xor_27_out), .b(xor_28_out), .c(in_1[5]), .x(out_3));
  \Мажоритарный_элемент_на_три_входа  \u_мажоритарный_элемент_на_три_входа_11  (
    .a(xor_29_out), .b(xor_30_out), .c(in_1[4]), .x(out_4));
  \Мажоритарный_элемент_на_три_входа  \u_мажоритарный_элемент_на_три_входа_12  (
    .a(xor_31_out), .b(xor_32_out), .c(in_1[3]), .x(out_5));
endmodule
