// Logisim project пз.circ as structural Verilog: 1 circuit, main circuit main
module main (
  input  i1,
  input  in_2,
  input  i2,
  input  in_4,
  input  i3,
  input  in_6,
  input  i4,
  input  in_8,
  input  in_9,
  input  in_10,
  input  in_11
);

  wire xor_1_out, xor_2_out, xor_3_out;

  xor xor_1 (xor_1_out, i1, i2, i4);
  xor xor_2 (xor_2_out, i1, i3, i4);
  xor xor_3 (xor_3_out, i2, i3, i4);
endmodule
